// Digital circuit 8_BIT_MULTIPLIER.dig as structural Verilog
module _8_BIT_MULTIPLIER (
  input  [7:0] A,
  input  [7:0] B,
  output [15:0] SUM
);

  wire row_0_1_fa, row_0_1_fa_2, row_0_1_fa_3, row_0_1_fa_4, row_0_1_fa_5, row_0_1_fa_6, row_0_1_ha,
       row_1_1_fa, row_1_1_fa_2, row_1_1_fa_3, row_1_1_fa_4, row_1_1_fa_5, row_1_1_fa_6, row_1_1_fa_7,
       row_1_1_ha_out, row_2_1_fa, row_2_1_fa_2, row_2_1_fa_3, row_2_1_fa_4, row_2_1_fa_5, row_2_1_fa_6,
       row_2_1_fa_7, row_2_1_ha_out, row_3_1_fa, row_3_1_fa_2, row_3_1_fa_3, row_3_1_fa_4, row_3_1_fa_5,
       row_3_1_fa_6, row_3_1_fa_7, row_3_1_ha_out, row_4_1_fa, row_4_1_fa_2, row_4_1_fa_3, row_4_1_fa_4,
       row_4_1_fa_5, row_4_1_fa_6, row_4_1_fa_7, row_4_1_ha_out, row_5_1_fa, row_5_1_fa_2, row_5_1_fa_3,
       row_5_1_fa_4, row_5_1_fa_5, row_5_1_fa_6, row_5_1_fa_7, row_5_1_ha_out, row_6_1_fa, row_6_1_fa_2,
       row_6_1_fa_3, row_6_1_fa_4, row_6_1_fa_5, row_6_1_fa_6, row_6_1_fa_7, row_6_1_ha_out;

  ROW_0 row_0_1 (
    .B_0(B[0]), .FA_6(row_0_1_fa_6), .FA_5(row_0_1_fa_5), .FA_4(row_0_1_fa_4), .FA_3(row_0_1_fa_3),
    .FA_2(row_0_1_fa_2), .FA(row_0_1_fa), .HA(row_0_1_ha), .P0(SUM[0]), .A_7(A[7]), .A_6(A[6]), .A_5(A[5]),
    .A_4(A[4]), .A_3(A[3]), .A_2(A[2]), .A_1(A[1]), .A_0(A[0]));
  ROW_1 row_1_1 (
    .B_1(B[1]), .HA(row_0_1_ha), .FA_IN(row_0_1_fa), .FA_IN_2(row_0_1_fa_2), .FA_IN_3(row_0_1_fa_3),
    .FA_IN_4(row_0_1_fa_4), .FA_IN_5(row_0_1_fa_5), .FA_IN_6(row_0_1_fa_6), .A_0(A[0]), .A_1(A[1]),
    .A_2(A[2]), .A_3(A[3]), .A_4(A[4]), .A_5(A[5]), .A_6(A[6]), .A_7(A[7]), .P1(SUM[1]),
    .HA_OUT(row_1_1_ha_out), .FA(row_1_1_fa), .FA_2(row_1_1_fa_2), .FA_3(row_1_1_fa_3), .FA_4(row_1_1_fa_4),
    .FA_5(row_1_1_fa_5), .FA_6(row_1_1_fa_6), .FA_7(row_1_1_fa_7));
  ROW_2 row_2_1 (
    .B_2(B[2]), .HA(row_1_1_ha_out), .FA_IN(row_1_1_fa), .FA_IN_2(row_1_1_fa_2), .FA_IN_3(row_1_1_fa_3),
    .FA_IN_4(row_1_1_fa_4), .FA_IN_5(row_1_1_fa_5), .FA_IN_6(row_1_1_fa_6), .FA_IN_7(row_1_1_fa_7),
    .A_0(A[0]), .A_1(A[1]), .A_2(A[2]), .A_3(A[3]), .A_4(A[4]), .A_5(A[5]), .A_6(A[6]), .A_7(A[7]),
    .P2(SUM[2]), .HA_OUT(row_2_1_ha_out), .FA(row_2_1_fa), .FA_2(row_2_1_fa_2), .FA_3(row_2_1_fa_3),
    .FA_4(row_2_1_fa_4), .FA_5(row_2_1_fa_5), .FA_6(row_2_1_fa_6), .FA_7(row_2_1_fa_7));
  ROW_3 row_3_1 (
    .B_3(B[3]), .HA(row_2_1_ha_out), .FA_IN(row_2_1_fa), .FA_IN_2(row_2_1_fa_2), .FA_IN_3(row_2_1_fa_3),
    .FA_IN_4(row_2_1_fa_4), .FA_IN_5(row_2_1_fa_5), .FA_IN_6(row_2_1_fa_6), .FA_IN_7(row_2_1_fa_7),
    .A_0(A[0]), .A_1(A[1]), .A_2(A[2]), .A_3(A[3]), .A_4(A[4]), .A_5(A[5]), .A_6(A[6]), .A_7(A[7]),
    .P3(SUM[3]), .HA_OUT(row_3_1_ha_out), .FA(row_3_1_fa), .FA_2(row_3_1_fa_2), .FA_3(row_3_1_fa_3),
    .FA_4(row_3_1_fa_4), .FA_5(row_3_1_fa_5), .FA_6(row_3_1_fa_6), .FA_7(row_3_1_fa_7));
  ROW_4 row_4_1 (
    .B_4(B[4]), .HA(row_3_1_ha_out), .FA_IN(row_3_1_fa), .FA_IN_2(row_3_1_fa_2), .FA_IN_3(row_3_1_fa_3),
    .FA_IN_4(row_3_1_fa_4), .FA_IN_5(row_3_1_fa_5), .FA_IN_6(row_3_1_fa_6), .FA_IN_7(row_3_1_fa_7),
    .A_0(A[0]), .A_1(A[1]), .A_2(A[2]), .A_3(A[3]), .A_4(A[4]), .A_5(A[5]), .A_6(A[6]), .A_7(A[7]),
    .P4(SUM[4]), .HA_OUT(row_4_1_ha_out), .FA(row_4_1_fa), .FA_2(row_4_1_fa_2), .FA_3(row_4_1_fa_3),
    .FA_4(row_4_1_fa_4), .FA_5(row_4_1_fa_5), .FA_6(row_4_1_fa_6), .FA_7(row_4_1_fa_7));
  ROW_5 row_5_1 (
    .B_5(B[5]), .HA(row_4_1_ha_out), .FA_IN(row_4_1_fa), .FA_IN_2(row_4_1_fa_2), .FA_IN_3(row_4_1_fa_3),
    .FA_IN_4(row_4_1_fa_4), .FA_IN_5(row_4_1_fa_5), .FA_IN_6(row_4_1_fa_6), .FA_IN_7(row_4_1_fa_7),
    .A_0(A[0]), .A_1(A[1]), .A_2(A[2]), .A_3(A[3]), .A_4(A[4]), .A_5(A[5]), .A_6(A[6]), .A_7(A[7]),
    .P5(SUM[5]), .HA_OUT(row_5_1_ha_out), .FA(row_5_1_fa), .FA_2(row_5_1_fa_2), .FA_3(row_5_1_fa_3),
    .FA_4(row_5_1_fa_4), .FA_5(row_5_1_fa_5), .FA_6(row_5_1_fa_6), .FA_7(row_5_1_fa_7));
  ROW_6 row_6_1 (
    .B_6(B[6]), .HA(row_5_1_ha_out), .FA_IN(row_5_1_fa), .FA_IN_2(row_5_1_fa_2), .FA_IN_3(row_5_1_fa_3),
    .FA_IN_4(row_5_1_fa_4), .FA_IN_5(row_5_1_fa_5), .FA_IN_6(row_5_1_fa_6), .FA_IN_7(row_5_1_fa_7),
    .A_0(A[0]), .A_1(A[1]), .A_2(A[2]), .A_3(A[3]), .A_4(A[4]), .A_5(A[5]), .A_6(A[6]), .A_7(A[7]),
    .P6(SUM[6]), .HA_OUT(row_6_1_ha_out), .FA(row_6_1_fa), .FA_2(row_6_1_fa_2), .FA_3(row_6_1_fa_3),
    .FA_4(row_6_1_fa_4), .FA_5(row_6_1_fa_5), .FA_6(row_6_1_fa_6), .FA_7(row_6_1_fa_7));
  ROW_7 row_7_1 (
    .B_7(B[7]), .HA(row_6_1_ha_out), .FA_IN(row_6_1_fa), .FA_IN_2(row_6_1_fa_2), .FA_IN_3(row_6_1_fa_3),
    .FA_IN_4(row_6_1_fa_4), .FA_IN_5(row_6_1_fa_5), .FA_IN_6(row_6_1_fa_6), .FA_IN_7(row_6_1_fa_7),
    .A_0(A[0]), .A_1(A[1]), .A_2(A[2]), .A_3(A[3]), .A_4(A[4]), .A_5(A[5]), .A_6(A[6]), .A_7(A[7]),
    .P7(SUM[7]), .P8(SUM[8]), .P9(SUM[9]), .P10(SUM[10]), .P11(SUM[11]), .P12(SUM[12]), .P13(SUM[13]),
    .P14(SUM[14]), .P15(SUM[15]));
endmodule
