// Digital circuit 8_BIT_RIPPLE_CARRY_ADDER.dig as structural Verilog
module _8_BIT_RIPPLE_CARRY_ADDER (
  input  [7:0] A,
  input  [7:0] B,
  output SUM_0,
  output SUM_1,
  output SUM_2,
  output SUM_3,
  output SUM_4,
  output SUM_5,
  output SUM_6,
  output SUM_7,
  output CARRY
);

  wire full_adder_1_carry, full_adder_2_carry, full_adder_3_carry, full_adder_4_carry, full_adder_5_carry,
       full_adder_6_carry, half_adder_1_sum;

  HALF_ADDER half_adder_1 (.A(A[0]), .B(B[0]), .SUM(half_adder_1_sum), .CARRY(SUM_0));
  FULL_ADDER full_adder_1 (.A(half_adder_1_sum), .B(A[1]), .C(B[1]), .SUM(SUM_1), .CARRY(full_adder_1_carry));
  FULL_ADDER full_adder_2 (.A(full_adder_1_carry), .B(A[2]), .C(B[2]), .SUM(SUM_2), .CARRY(full_adder_2_carry));
  FULL_ADDER full_adder_3 (.A(full_adder_2_carry), .B(A[3]), .C(B[3]), .SUM(SUM_3), .CARRY(full_adder_3_carry));
  FULL_ADDER full_adder_4 (.A(full_adder_3_carry), .B(A[4]), .C(B[4]), .SUM(SUM_4), .CARRY(full_adder_4_carry));
  FULL_ADDER full_adder_5 (.A(full_adder_4_carry), .B(A[5]), .C(B[5]), .SUM(SUM_5), .CARRY(full_adder_5_carry));
  FULL_ADDER full_adder_6 (.A(full_adder_5_carry), .B(A[6]), .C(B[6]), .SUM(SUM_6), .CARRY(full_adder_6_carry));
  FULL_ADDER full_adder_7 (.A(full_adder_6_carry), .B(A[7]), .C(B[7]), .SUM(SUM_7), .CARRY(CARRY));
endmodule
