// Digital circuit FULL_ADDER.dig as structural Verilog
module FULL_ADDER (
  input  A,
  input  B,
  input  C,
  output SUM,
  output CARRY
);

  wire half_adder_1_carry, half_adder_1_sum, half_adder_2_sum;

  HALF_ADDER half_adder_1 (.A(A), .B(B), .SUM(half_adder_1_sum), .CARRY(half_adder_1_carry));
  HALF_ADDER half_adder_2 (.A(half_adder_1_carry), .B(C), .SUM(half_adder_2_sum), .CARRY(CARRY));
  or or_1 (SUM, half_adder_1_sum, half_adder_2_sum);
endmodule
