// Digital circuit 2_BIT_DIVIDER.dig as structural Verilog
module _2_BIT_DIVIDER (
  input  A_0,
  input  A_1,
  input  B_0,
  input  B_1,
  output C_0,
  output C_1,
  output C_2,
  output C_3
);

  wire and_1_out, and_3_out, and_4_out, and_5_out;

  and and_1 (and_1_out, A_0, B_1);
  and and_2 (C_0, A_0, B_0);
  and and_3 (and_3_out, A_1, B_0);
  and and_4 (and_4_out, A_1, B_1);
  xor xor_1 (C_1, and_1_out, and_3_out);
  and and_5 (and_5_out, and_1_out, and_3_out);
  xor xor_2 (C_2, and_5_out, and_4_out);
  and and_6 (C_3, and_5_out, and_4_out);
endmodule
