// Digital circuit 8_BIT_ADDER_SUBTRACTOR.dig as structural Verilog
module _8_BIT_ADDER_SUBTRACTOR (
  input  [7:0] A,
  input  [7:0] B,
  input  MODE,
  output CARRY_OUT,
  output [7:0] SUM
);

  wire full_adder_2_sum, full_adder_3_sum, full_adder_4_sum, full_adder_5_sum, full_adder_6_sum,
       full_adder_7_sum, full_adder_8_sum, xor_1_out, xor_2_out, xor_3_out, xor_4_out, xor_5_out, xor_6_out,
       xor_7_out, xor_8_out;

  xor xor_1 (xor_1_out, B[7], MODE);
  FULL_ADDER full_adder_1 (.A(A[7]), .B(xor_1_out), .C(full_adder_2_sum), .SUM(CARRY_OUT), .CARRY(SUM[7]));
  xor xor_2 (xor_2_out, B[6], MODE);
  FULL_ADDER full_adder_2 (.A(A[6]), .B(xor_2_out), .C(full_adder_3_sum), .SUM(full_adder_2_sum), .CARRY(SUM[6]));
  xor xor_3 (xor_3_out, B[5], MODE);
  FULL_ADDER full_adder_3 (.A(A[5]), .B(xor_3_out), .C(full_adder_4_sum), .SUM(full_adder_3_sum), .CARRY(SUM[5]));
  xor xor_4 (xor_4_out, B[4], MODE);
  FULL_ADDER full_adder_4 (.A(A[4]), .B(xor_4_out), .C(full_adder_5_sum), .SUM(full_adder_4_sum), .CARRY(SUM[4]));
  xor xor_5 (xor_5_out, B[3], MODE);
  FULL_ADDER full_adder_5 (.A(A[3]), .B(xor_5_out), .C(full_adder_6_sum), .SUM(full_adder_5_sum), .CARRY(SUM[3]));
  xor xor_6 (xor_6_out, B[2], MODE);
  FULL_ADDER full_adder_6 (.A(A[2]), .B(xor_6_out), .C(full_adder_7_sum), .SUM(full_adder_6_sum), .CARRY(SUM[2]));
  xor xor_7 (xor_7_out, B[1], MODE);
  FULL_ADDER full_adder_7 (.A(A[1]), .B(xor_7_out), .C(full_adder_8_sum), .SUM(full_adder_7_sum), .CARRY(SUM[1]));
  xor xor_8 (xor_8_out, B[0], MODE);
  FULL_ADDER full_adder_8 (.A(A[0]), .B(xor_8_out), .C(MODE), .SUM(full_adder_8_sum), .CARRY(SUM[0]));
endmodule
