// Digital circuit 8_BIT_DECREMENTER.dig as structural Verilog
module _8_BIT_DECREMENTER (
  input  [7:0] A,
  output BORROW_OUT,
  output [7:0] A_B
);

  _8_BIT_SUBTRACTOR _8_bit_subtractor_1 (.A(A), .B(8'h1), .A_B(A_B), .BORROW_OUT(BORROW_OUT));
endmodule
