// Digital circuit 8_BIT_RIPPLE_ADDER.dig as structural Verilog
module _8_BIT_RIPPLE_ADDER (
  input  [7:0] A,
  input  [7:0] B,
  output OVERFLOW,
  output [7:0] A_PLUS_B
);

  wire full_adder_1_carry, full_adder_2_carry, full_adder_3_carry, full_adder_4_carry, full_adder_5_carry,
       full_adder_6_carry, full_adder_7_carry;

  FULL_ADDER full_adder_1 (.A(A[0]), .B(B[0]), .C(1'b0), .SUM(A_PLUS_B[0]), .CARRY(full_adder_1_carry));
  FULL_ADDER full_adder_2 (.A(A[1]), .B(B[1]), .C(full_adder_1_carry), .SUM(A_PLUS_B[1]), .CARRY(full_adder_2_carry));
  FULL_ADDER full_adder_3 (.A(A[2]), .B(B[2]), .C(full_adder_2_carry), .SUM(A_PLUS_B[2]), .CARRY(full_adder_3_carry));
  FULL_ADDER full_adder_4 (.A(A[3]), .B(B[3]), .C(full_adder_3_carry), .SUM(A_PLUS_B[3]), .CARRY(full_adder_4_carry));
  FULL_ADDER full_adder_5 (.A(A[4]), .B(B[4]), .C(full_adder_4_carry), .SUM(A_PLUS_B[4]), .CARRY(full_adder_5_carry));
  FULL_ADDER full_adder_6 (.A(A[5]), .B(B[5]), .C(full_adder_5_carry), .SUM(A_PLUS_B[5]), .CARRY(full_adder_6_carry));
  FULL_ADDER full_adder_7 (.A(A[6]), .B(B[6]), .C(full_adder_6_carry), .SUM(A_PLUS_B[6]), .CARRY(full_adder_7_carry));
  FULL_ADDER full_adder_8 (.A(A[7]), .B(B[7]), .C(full_adder_7_carry), .SUM(A_PLUS_B[7]), .CARRY(OVERFLOW));
endmodule
