// Digital circuit 8_BIT_RIPPLE_ADDER_FIXED.dig as structural Verilog
module _8_BIT_RIPPLE_ADDER_FIXED (
  input  [7:0] A,
  input  [7:0] B,
  input  CARRY_IN,
  output CARRY_OUT,
  output OVERFLOW,
  output [7:0] A_PLUS_B
);

  wire undriven, undriven_2, undriven_3, undriven_4, undriven_5, undriven_6, undriven_7;

  FULL_ADDER full_adder_1 (.A(A[0]), .B(B[0]), .C(CARRY_IN));  // open: SUM, CARRY
  FULL_ADDER full_adder_2 (.A(A[1]), .B(B[1]), .C(undriven_7));  // open: SUM, CARRY
  FULL_ADDER full_adder_3 (.A(A[2]), .B(B[2]), .C(undriven_6));  // open: SUM, CARRY
  FULL_ADDER full_adder_4 (.A(A[3]), .B(B[3]), .C(undriven));  // open: SUM, CARRY
  FULL_ADDER full_adder_5 (.A(A[4]), .B(B[4]), .C(undriven_2));  // open: SUM, CARRY
  FULL_ADDER full_adder_6 (.A(A[5]), .B(B[5]), .C(undriven_3));  // open: SUM, CARRY
  FULL_ADDER full_adder_7 (.A(A[6]), .B(B[6]), .C(undriven_4));  // open: SUM, CARRY
  FULL_ADDER full_adder_8 (.A(A[7]), .B(B[7]), .C(undriven_5));  // open: SUM, CARRY
  // XOr xor_1 is placed but not wired
endmodule
