// Digital circuit 8_BIT_SUBTRACTOR.dig as structural Verilog
module _8_BIT_SUBTRACTOR (
  input  [7:0] A,
  input  [7:0] B,
  output [7:0] A_B,
  output BORROW_OUT
);

  wire full_subtractor_1_b_out, full_subtractor_2_b_out, full_subtractor_3_b_out, full_subtractor_4_b_out,
       full_subtractor_5_b_out, full_subtractor_6_b_out, half_subtractor_1_borrow;

  HALF_SUBTRACTOR half_subtractor_1 (.A(A[0]), .B(B[0]), .DIFFERENCE(A_B[0]), .BORROW(half_subtractor_1_borrow));
  FULL_SUBTRACTOR full_subtractor_1 (
    .B_IN(half_subtractor_1_borrow), .A(A[1]), .B(B[1]), .DIFF(A_B[1]), .B_OUT(full_subtractor_1_b_out));
  FULL_SUBTRACTOR full_subtractor_2 (
    .B_IN(full_subtractor_1_b_out), .A(A[2]), .B(B[2]), .DIFF(A_B[2]), .B_OUT(full_subtractor_2_b_out));
  FULL_SUBTRACTOR full_subtractor_3 (
    .B_IN(full_subtractor_2_b_out), .A(A[3]), .B(B[3]), .DIFF(A_B[3]), .B_OUT(full_subtractor_3_b_out));
  FULL_SUBTRACTOR full_subtractor_4 (
    .B_IN(full_subtractor_3_b_out), .A(A[4]), .B(B[4]), .DIFF(A_B[4]), .B_OUT(full_subtractor_4_b_out));
  FULL_SUBTRACTOR full_subtractor_5 (
    .B_IN(full_subtractor_4_b_out), .A(A[5]), .B(B[5]), .DIFF(A_B[5]), .B_OUT(full_subtractor_5_b_out));
  FULL_SUBTRACTOR full_subtractor_6 (
    .B_IN(full_subtractor_5_b_out), .A(A[6]), .B(B[6]), .DIFF(A_B[6]), .B_OUT(full_subtractor_6_b_out));
  FULL_SUBTRACTOR full_subtractor_7 (
    .B_IN(full_subtractor_6_b_out), .A(A[7]), .B(B[7]), .DIFF(A_B[7]), .B_OUT(BORROW_OUT));
endmodule
