// Digital circuit 8_BIT_X_8_BIT_NON_RESTORING_ARRAY_DIVIDER.dig as structural Verilog
module _8_BIT_X_8_BIT_NON_RESTORING_ARRAY_DIVIDER (
  input  P
);

  // CAS_UNIT cas_unit_1: pin names not known; wires that end beside it: P
endmodule
