// Digital circuit CAS_UNIT.dig as structural Verilog
module CAS_UNIT (
  input  P,
  input  D_IN,
  input  C_IN,
  input  R_IN,
  output C_OUT,
  output R_OUT,
  output D_OUT
);

  wire xor_1_out;

  xor xor_1 (xor_1_out, P, D_IN);
  FULL_ADDER full_adder_1 (.A(xor_1_out), .B(R_IN), .C(C_IN), .SUM(C_OUT), .CARRY(R_OUT));

  assign D_OUT = D_IN;
endmodule
