// Digital circuit FULL_ADDER.dig as structural Verilog
module FULL_ADDER (
  input  A,
  input  B,
  input  C,
  output SUM,
  output CARRY
);

  wire half_adder_1_carry, half_adder_1_sum, half_adder_2_carry;

  HALF_ADDER half_adder_1 (.A(A), .B(B), .SUM(half_adder_1_sum), .CARRY(half_adder_1_carry));
  HALF_ADDER half_adder_2 (.A(C), .B(half_adder_1_sum), .SUM(SUM), .CARRY(half_adder_2_carry));
  or or_1 (CARRY, half_adder_2_carry, half_adder_1_carry);
endmodule
