// Digital circuit PU.dig as structural Verilog
module PU (
  input  A,
  input  SEL,
  input  B,
  input  C_IN,
  output Y,
  output C_OUT
);

  wire and_1_out, and_2_out, full_adder_1_sum, not_1_out, not_2_out;

  or or_1 (Y, and_2_out, and_1_out);
  not not_1 (not_1_out, B);
  and and_1 (and_1_out, SEL, full_adder_1_sum);
  and and_2 (and_2_out, not_2_out, A);
  FULL_ADDER full_adder_1 (.A(A), .B(not_1_out), .C(C_IN), .SUM(full_adder_1_sum), .CARRY(C_OUT));
  not not_2 (not_2_out, SEL);
endmodule
