// Digital circuit ARITHMETUC_UNIT.dig as structural Verilog
module ARITHMETUC_UNIT (
  output out_1
);

  _8_BIT_RIPPLE_ADDER _8_bit_ripple_adder_1 ();  // open: A, B, OVERFLOW, A_PLUS_B
  _8_BIT_SUBTRACTOR _8_bit_subtractor_1 ();  // open: A, B, A_B, BORROW_OUT
  _8_BIT_INCREMENTER _8_bit_incrementer_1 ();  // open: A, A_plus_1, OVERFLOW
  _8_BIT_DECREMENTER _8_bit_decrementer_1 ();  // open: A, BORROW_OUT, A_B
  _8_BIT_ADDER_SUBTRACTOR _8_bit_adder_subtractor_1 ();  // open: A, B, MODE, CARRY_OUT, SUM
  _8_BIT_MULTIPLIER _8_bit_multiplier_1 ();  // open: A, B, SUM
endmodule
