// Digital circuit 1X16_MULTIPLEXER.dig as structural Verilog
module _1X16_MULTIPLEXER (
  input  S_0,
  input  S_1,
  input  S_2,
  input  S_3,
  input  D_0,
  input  D_1,
  input  D_2,
  input  D_3,
  input  D_4,
  input  D_5,
  input  D_6,
  input  D_7,
  input  D_8,
  input  D_9,
  input  D_10,
  input  D_11,
  input  D_12,
  input  D_13,
  input  D_14,
  input  D_15
);

  // Not not_1 is placed but not wired
  // Not not_2 is placed but not wired
  // Not not_3 is placed but not wired
  // Not not_4 is placed but not wired
  // And and_1 is placed but not wired
endmodule
