// Digital circuit 2X1_MULTIPLEXER.dig as structural Verilog
module _2X1_MULTIPLEXER (
  input  SEL,
  input  D_0,
  input  D_1,
  output Y
);

  wire and_1_out, and_2_out, not_1_out;

  not not_1 (not_1_out, SEL);
  and and_1 (and_1_out, not_1_out, D_0);
  and and_2 (and_2_out, SEL, D_1);
  or or_1 (Y, and_1_out, and_2_out);
endmodule
