// Digital circuit 8X1_MULTIPLEXER.dig as structural Verilog
module _8X1_MULTIPLEXER (
  input  S_0,
  input  S_1,
  input  S_2,
  input  D_0,
  input  D_1,
  input  D_2,
  input  D_3,
  input  D_4,
  input  D_5,
  input  D_6,
  input  D_7,
  output Y
);

  wire _4x1_multiplexer_1_y, _4x1_multiplexer_2_y;

  _4X1_MULTIPLEXER _4x1_multiplexer_1 (
    .S_0(S_0), .S_1(S_1), .D_0(D_0), .D_1(D_1), .D_2(D_2), .D_3(D_3), .Y(_4x1_multiplexer_1_y));
  _4X1_MULTIPLEXER _4x1_multiplexer_2 (
    .S_0(S_0), .S_1(S_1), .D_0(D_4), .D_1(D_5), .D_2(D_6), .D_3(D_7), .Y(_4x1_multiplexer_2_y));
  _2x1_MULTIPLEXER _2x1_multiplexer_1 (.SEL(S_2), .D_0(_4x1_multiplexer_1_y), .D_1(_4x1_multiplexer_2_y), .Y(Y));
endmodule
