// Digital circuit 1X16_DEMULTIPLEXER_MIRRORED.dig as structural Verilog
module _1X16_DEMULTIPLEXER_MIRRORED (
  input  IN,
  input  S_3,
  input  S_0,
  input  S_1,
  input  S_2,
  output D_0,
  output D_1,
  output D_2,
  output D_3,
  output D_4,
  output D_5,
  output D_6,
  output D_7,
  output D_8,
  output D_9,
  output D_10,
  output D_11,
  output D_12,
  output D_13,
  output D_14,
  output D_15
);

  wire _1x2_demultiplexer_1_p3, _1x2_demultiplexer_1_p4;

  // _1X2_DEMULTIPLEXER _1x2_demultiplexer_1: pin names not known; wires that end beside it: IN, S_3, _1x2_demultiplexer_1_p3, _1x2_demultiplexer_1_p4
  _1X8_DEMULTIPLEXER _1x8_demultiplexer_1 (
    .S_2(S_2), .S_1(S_1), .S_0(S_0), .IN(_1x2_demultiplexer_1_p3), .D_0(D_0), .D_1(D_1), .D_2(D_2),
    .D_3(D_3), .D_4(D_4), .D_5(D_5), .D_6(D_6), .D_7(D_7));
  _1X8_DEMULTIPLEXER _1x8_demultiplexer_2 (
    .S_2(S_2), .S_1(S_1), .S_0(S_0), .IN(_1x2_demultiplexer_1_p4), .D_0(D_8), .D_1(D_9), .D_2(D_10),
    .D_3(D_11), .D_4(D_12), .D_5(D_13), .D_6(D_14), .D_7(D_15));
endmodule
