// Digital circuit CLK_TRANSITION_DETECTION_CIRCUIT.dig as structural Verilog
module CLK_TRANSITION_DETECTION_CIRCUIT (
  input  CLK,
  output OUT
);

  wire not_1_out;

  not not_1 (not_1_out, CLK);
  and and_1 (OUT, not_1_out, CLK);
endmodule
