// Digital circuit DFF.dig as structural Verilog
module DFF (
  input  D,
  input  CLK,
  output Q,
  output Q_2
);

  wire not_1_out;

  not not_1 (not_1_out, D);
  GATED_SR_LATCH_W_NAND gated_sr_latch_w_nand_1 (.S(D), .CLK(CLK), .R(not_1_out), .Q(Q), .Q_2(Q_2));
endmodule
