// Digital circuit GATED_D_LATCH.dig as structural Verilog
module GATED_D_LATCH (
  input  D,
  input  ENB,
  output Q,
  output Q_2
);

  wire and_1_out, and_2_out, not_1_out;

  not not_1 (not_1_out, D);
  and and_1 (and_1_out, not_1_out, ENB);
  and and_2 (and_2_out, ENB, D);
  nor nor_1 (Q, and_1_out, Q_2);
  nor nor_2 (Q_2, Q, and_2_out);
endmodule
