// Digital circuit GATED_SR.dig as structural Verilog
module GATED_SR (
  input  WR,
  input  IN,
  output OUT
);

  wire and_1_out, and_2_out, not_1_out, not_2_out, or_1_out;

  and and_1 (and_1_out, IN, WR);
  and and_2 (and_2_out, not_1_out, WR);
  not not_1 (not_1_out, IN);
  or or_1 (or_1_out, OUT, and_1_out);
  not not_2 (not_2_out, and_2_out);
  and and_3 (OUT, or_1_out, not_2_out);
endmodule
