// Digital circuit GATED_SR_LATCH_W_NAND.dig as structural Verilog
module GATED_SR_LATCH_W_NAND (
  input  S,
  input  CLK,
  input  R,
  output Q,
  output Q_2
);

  wire nand_1_out, nand_2_out;

  nand nand_1 (nand_1_out, S, CLK);
  nand nand_2 (nand_2_out, CLK, R);
  nand nand_3 (Q, nand_1_out, Q_2);
  nand nand_4 (Q_2, Q, nand_2_out);
endmodule
