// Digital circuit GATED_SR_LATCH_W_NOR.dig as structural Verilog
module GATED_SR_LATCH_W_NOR (
  input  R,
  input  S,
  input  CLK,
  output Q,
  output Q_2
);

  wire and_1_out, and_2_out;

  and and_1 (and_1_out, R, CLK);
  and and_2 (and_2_out, CLK, S);
  nor nor_1 (Q, and_1_out, Q_2);
  nor nor_2 (Q_2, Q, and_2_out);

  // Notes on the sheet:
  //   Q_(n+1) = S + R'Q_n
endmodule
