// Digital circuit MASTER_SLAVE_JK.dig as structural Verilog
module MASTER_SLAVE_JK (
  input  CLK,
  input  J,
  input  K,
  output Q_BAR,
  output Q
);

  wire and_1_out, and_2_out;

  and and_1 (and_1_out, Q, J, CLK);
  and and_2 (and_2_out, CLK, K, Q_BAR);
  nand nand_1 (Q_BAR, and_1_out, Q);
  nand nand_2 (Q, Q_BAR, and_2_out);
endmodule
