// Digital circuit SR_LATCH.dig as structural Verilog
module SR_LATCH (
  input  SET,
  input  RESET,
  output OUT
);

  wire not_1_out, or_1_out;

  or or_1 (or_1_out, OUT, SET);
  not not_1 (not_1_out, RESET);
  and and_1 (OUT, or_1_out, not_1_out);
endmodule
