// Digital circuit ROW_0.dig as structural Verilog
module ROW_0 (
  input  B_0,
  input  A_1,
  input  A_0,
  input  A_2,
  input  A_3,
  input  A_5,
  input  A_4,
  input  A_6,
  input  A_7,
  output P0,
  output HA,
  output FA,
  output FA_2,
  output FA_3,
  output FA_4,
  output FA_5,
  output FA_6
);

  and and_1 (FA_6, B_0, A_7);
  and and_2 (FA_5, B_0, A_6);
  and and_3 (FA_4, B_0, A_5);
  and and_4 (FA_3, B_0, A_4);
  and and_5 (FA_2, B_0, A_3);
  and and_6 (FA, B_0, A_2);
  and and_7 (HA, B_0, A_1);
  and and_8 (P0, B_0, A_0);
endmodule
