// Digital circuit 8_BIT_REGISTER.dig as structural Verilog
module _8_BIT_REGISTER (
  input  ENB,
  input  IN_0,
  input  IN_1,
  input  IN_2,
  input  IN_3,
  input  IN_4,
  input  IN_5,
  input  IN_6,
  input  IN_7,
  output OUT_1,
  output OUT_2,
  output OUT_3,
  output OUT_4,
  output OUT_5,
  output OUT_6,
  output OUT_7,
  output OUT_8
);

  GATED_SR gated_sr_1 (.WR(ENB), .IN(IN_0), .OUT(OUT_1));
  GATED_SR gated_sr_2 (.WR(ENB), .IN(IN_1), .OUT(OUT_2));
  GATED_SR gated_sr_3 (.WR(ENB), .IN(IN_2), .OUT(OUT_3));
  GATED_SR gated_sr_4 (.WR(ENB), .IN(IN_3), .OUT(OUT_4));
  GATED_SR gated_sr_5 (.WR(ENB), .IN(IN_4), .OUT(OUT_5));
  GATED_SR gated_sr_6 (.WR(ENB), .IN(IN_5), .OUT(OUT_6));
  GATED_SR gated_sr_7 (.WR(ENB), .IN(IN_6), .OUT(OUT_7));
  GATED_SR gated_sr_8 (.WR(ENB), .IN(IN_7), .OUT(OUT_8));
endmodule
