// Digital circuit 4X16_LATCH_MATRIX.dig as structural Verilog
module _4X16_LATCH_MATRIX (
  input  IN,
  input  READ,
  input  WR,
  input  R_0,
  input  R_1,
  input  R_2,
  input  R_3,
  input  R_4,
  input  R_5,
  input  R_6,
  input  R_7,
  input  R_8,
  input  R_9,
  input  R_10,
  input  R_11,
  input  R_12,
  input  R_13,
  input  R_14,
  input  R_15,
  input  C_0,
  input  C_1,
  input  C_2,
  input  C_3,
  output OUT
);

  wire _4x4_latch_matrix_1_out, _4x4_latch_matrix_2_out, _4x4_latch_matrix_3_out, _4x4_latch_matrix_4_out;

  _4x4_LATCH_MATRIX _4x4_latch_matrix_1 (
    .IN(IN), .READ(READ), .WR(WR), .R_0(R_0), .R_1(R_1), .R_2(R_2), .R_3(R_3), .C_0(C_0), .C_1(C_1),
    .C_2(C_2), .C_3(C_3), .OUT(_4x4_latch_matrix_1_out));
  _4x4_LATCH_MATRIX _4x4_latch_matrix_2 (
    .IN(IN), .READ(READ), .WR(WR), .R_0(R_4), .R_1(R_5), .R_2(R_6), .R_3(R_7), .C_0(C_0), .C_1(C_1),
    .C_2(C_2), .C_3(C_3), .OUT(_4x4_latch_matrix_2_out));
  _4x4_LATCH_MATRIX _4x4_latch_matrix_3 (
    .IN(IN), .READ(READ), .WR(WR), .R_0(R_8), .R_1(R_9), .R_2(R_10), .R_3(R_11), .C_0(C_0), .C_1(C_1),
    .C_2(C_2), .C_3(C_3), .OUT(_4x4_latch_matrix_3_out));
  _4x4_LATCH_MATRIX _4x4_latch_matrix_4 (
    .IN(IN), .READ(READ), .WR(WR), .R_0(R_12), .R_1(R_13), .R_2(R_14), .R_3(R_15), .C_0(C_0), .C_1(C_1),
    .C_2(C_2), .C_3(C_3), .OUT(_4x4_latch_matrix_4_out));
  _4_BIT_IS_1 _4_bit_is_1_1 (
    .IN_0(_4x4_latch_matrix_1_out), .IN_1(_4x4_latch_matrix_2_out), .IN_2(_4x4_latch_matrix_3_out),
    .IN_3(_4x4_latch_matrix_4_out), .OUT(OUT));
endmodule
