// Digital circuit 4_BIT_IS_1.dig as structural Verilog
module _4_BIT_IS_1 (
  input  IN_0,
  input  IN_1,
  input  IN_2,
  input  IN_3,
  output OUT
);

  wire or_1_out, or_2_out;

  or or_1 (or_1_out, IN_0, IN_1);
  or or_2 (or_2_out, IN_2, IN_3);
  or or_3 (OUT, or_1_out, or_2_out);
endmodule
