// Digital circuit 16X1_MULTIPLEXER.dig as structural Verilog
module _16X1_MULTIPLEXER (
  input  S_1,
  input  S_0,
  input  D_0,
  input  D_1,
  input  D_2,
  input  D_3,
  input  D_4,
  input  D_5,
  input  D_6,
  input  D_7,
  input  D_8,
  input  D_9,
  input  D_10,
  input  D_11,
  input  D_12,
  input  D_13,
  input  D_14,
  input  D_15,
  input  S_2,
  input  S_3,
  output Y
);

  wire _4x1_multiplexer_1_y, _4x1_multiplexer_2_y, _4x1_multiplexer_3_y, _4x1_multiplexer_4_y;

  _4X1_MULTIPLEXER _4x1_multiplexer_1 (
    .S_1(S_1), .S_0(S_0), .D_0(D_0), .D_1(D_1), .D_2(D_2), .D_3(D_3), .Y(_4x1_multiplexer_1_y));
  _4X1_MULTIPLEXER _4x1_multiplexer_2 (
    .S_1(S_1), .S_0(S_0), .D_0(D_4), .D_1(D_5), .D_2(D_6), .D_3(D_7), .Y(_4x1_multiplexer_2_y));
  _4X1_MULTIPLEXER _4x1_multiplexer_3 (
    .S_1(S_1), .S_0(S_0), .D_0(D_8), .D_1(D_9), .D_2(D_10), .D_3(D_11), .Y(_4x1_multiplexer_3_y));
  _4X1_MULTIPLEXER _4x1_multiplexer_4 (
    .S_1(S_1), .S_0(S_0), .D_0(D_12), .D_1(D_13), .D_2(D_14), .D_3(D_15), .Y(_4x1_multiplexer_4_y));
  _4X1_MULTIPLEXER _4x1_multiplexer_5 (
    .S_1(S_3), .S_0(S_2), .D_0(_4x1_multiplexer_1_y), .D_1(_4x1_multiplexer_2_y), .D_2(_4x1_multiplexer_3_y),
    .D_3(_4x1_multiplexer_4_y), .Y(Y));
endmodule
