// Digital circuit 16x16_LATCH_MATRIX.dig as structural Verilog
module _16x16_LATCH_MATRIX (
  input  DATA_IN,
  input  READ_ENB,
  input  WR_ENB,
  input  RS_3,
  input  RS_2,
  input  RS_1,
  input  RS_0,
  input  CS_3,
  input  CS_2,
  input  CS_1,
  input  CS_0,
  output OUT
);

  wire _1x16_demultiplexer_1_d_0, _1x16_demultiplexer_1_d_1, _1x16_demultiplexer_1_d_2,
       _1x16_demultiplexer_1_d_3, _1x16_demultiplexer_1_d_4, _1x16_demultiplexer_1_d_5,
       _1x16_demultiplexer_1_d_6, _1x16_demultiplexer_1_d_7, _1x16_demultiplexer_1_d_8,
       _1x16_demultiplexer_1_d_9, _1x16_demultiplexer_1_d_10, _1x16_demultiplexer_1_d_11,
       _1x16_demultiplexer_1_d_12, _1x16_demultiplexer_1_d_13, _1x16_demultiplexer_1_d_14,
       _1x16_demultiplexer_1_d_15, _1x16_demultiplexer_mirrored_1_d_0, _1x16_demultiplexer_mirrored_1_d_1,
       _1x16_demultiplexer_mirrored_1_d_2, _1x16_demultiplexer_mirrored_1_d_3,
       _1x16_demultiplexer_mirrored_1_d_4, _1x16_demultiplexer_mirrored_1_d_5,
       _1x16_demultiplexer_mirrored_1_d_6, _1x16_demultiplexer_mirrored_1_d_7,
       _1x16_demultiplexer_mirrored_1_d_8, _1x16_demultiplexer_mirrored_1_d_9,
       _1x16_demultiplexer_mirrored_1_d_10, _1x16_demultiplexer_mirrored_1_d_11,
       _1x16_demultiplexer_mirrored_1_d_12, _1x16_demultiplexer_mirrored_1_d_13,
       _1x16_demultiplexer_mirrored_1_d_14, _1x16_demultiplexer_mirrored_1_d_15;

  _1X16_DEMULTIPLEXER _1x16_demultiplexer_1 (
    .IN(1'b1), .S_3(RS_3), .S_2(RS_2), .S_1(RS_1), .S_0(RS_0), .D_0(_1x16_demultiplexer_1_d_0),
    .D_1(_1x16_demultiplexer_1_d_1), .D_2(_1x16_demultiplexer_1_d_2), .D_3(_1x16_demultiplexer_1_d_3),
    .D_4(_1x16_demultiplexer_1_d_4), .D_5(_1x16_demultiplexer_1_d_5), .D_6(_1x16_demultiplexer_1_d_6),
    .D_7(_1x16_demultiplexer_1_d_7), .D_8(_1x16_demultiplexer_1_d_8), .D_9(_1x16_demultiplexer_1_d_9),
    .D_10(_1x16_demultiplexer_1_d_10), .D_11(_1x16_demultiplexer_1_d_11), .D_12(_1x16_demultiplexer_1_d_12),
    .D_13(_1x16_demultiplexer_1_d_13), .D_14(_1x16_demultiplexer_1_d_14), .D_15(_1x16_demultiplexer_1_d_15));
  MODULAR_16X16LATCH_MATRIX modular_16x16latch_matrix_1 (
    .IN(DATA_IN), .READ(READ_ENB), .WR(WR_ENB), .R_0(_1x16_demultiplexer_1_d_0),
    .R_1(_1x16_demultiplexer_1_d_1), .R_2(_1x16_demultiplexer_1_d_2), .R_3(_1x16_demultiplexer_1_d_3),
    .R_4(_1x16_demultiplexer_1_d_4), .R_5(_1x16_demultiplexer_1_d_5), .R_6(_1x16_demultiplexer_1_d_6),
    .R_7(_1x16_demultiplexer_1_d_7), .R_8(_1x16_demultiplexer_1_d_8), .R_9(_1x16_demultiplexer_1_d_9),
    .R_10(_1x16_demultiplexer_1_d_10), .R_11(_1x16_demultiplexer_1_d_11), .R_12(_1x16_demultiplexer_1_d_12),
    .R_13(_1x16_demultiplexer_1_d_13), .R_14(_1x16_demultiplexer_1_d_14), .R_15(_1x16_demultiplexer_1_d_15),
    .C_0(_1x16_demultiplexer_mirrored_1_d_0), .C_1(_1x16_demultiplexer_mirrored_1_d_1),
    .C_2(_1x16_demultiplexer_mirrored_1_d_2), .C_3(_1x16_demultiplexer_mirrored_1_d_3),
    .C_4(_1x16_demultiplexer_mirrored_1_d_4), .C_5(_1x16_demultiplexer_mirrored_1_d_5),
    .C_6(_1x16_demultiplexer_mirrored_1_d_6), .C_7(_1x16_demultiplexer_mirrored_1_d_7),
    .C_8(_1x16_demultiplexer_mirrored_1_d_8), .C_9(_1x16_demultiplexer_mirrored_1_d_9),
    .C_10(_1x16_demultiplexer_mirrored_1_d_10), .C_11(_1x16_demultiplexer_mirrored_1_d_11),
    .C_12(_1x16_demultiplexer_mirrored_1_d_12), .C_13(_1x16_demultiplexer_mirrored_1_d_13),
    .C_14(_1x16_demultiplexer_mirrored_1_d_14), .C_15(_1x16_demultiplexer_mirrored_1_d_15), .OUT(OUT));
  _1X16_DEMULTIPLEXER_MIRRORED _1x16_demultiplexer_mirrored_1 (
    .IN(1'b1), .S_3(CS_3), .S_2(CS_2), .S_1(CS_1), .S_0(CS_0), .D_15(_1x16_demultiplexer_mirrored_1_d_15),
    .D_14(_1x16_demultiplexer_mirrored_1_d_14), .D_13(_1x16_demultiplexer_mirrored_1_d_13),
    .D_12(_1x16_demultiplexer_mirrored_1_d_12), .D_11(_1x16_demultiplexer_mirrored_1_d_11),
    .D_10(_1x16_demultiplexer_mirrored_1_d_10), .D_9(_1x16_demultiplexer_mirrored_1_d_9),
    .D_8(_1x16_demultiplexer_mirrored_1_d_8), .D_7(_1x16_demultiplexer_mirrored_1_d_7),
    .D_6(_1x16_demultiplexer_mirrored_1_d_6), .D_5(_1x16_demultiplexer_mirrored_1_d_5),
    .D_4(_1x16_demultiplexer_mirrored_1_d_4), .D_3(_1x16_demultiplexer_mirrored_1_d_3),
    .D_2(_1x16_demultiplexer_mirrored_1_d_2), .D_1(_1x16_demultiplexer_mirrored_1_d_1),
    .D_0(_1x16_demultiplexer_mirrored_1_d_0));
endmodule
