// Digital circuit 1X4_DEMULTIPLEXER.dig as structural Verilog
module _1X4_DEMULTIPLEXER (
  input  S_1,
  input  S_0,
  input  IN,
  output D_0,
  output D_1,
  output D_2,
  output D_3
);

  wire not_1_out, not_2_out;

  not not_1 (not_1_out, S_1);
  not not_2 (not_2_out, S_0);
  and and_1 (D_0, not_1_out, not_2_out, IN);
  and and_2 (D_1, not_1_out, S_0, IN);
  and and_3 (D_2, S_1, not_2_out, IN);
  and and_4 (D_3, S_1, S_0, IN);
endmodule
