// Digital circuit 1X8_DEMULTIPLEXER.dig as structural Verilog
module _1X8_DEMULTIPLEXER (
  input  S_2,
  input  S_1,
  input  S_0,
  input  IN,
  output D_0,
  output D_1,
  output D_2,
  output D_3,
  output D_4,
  output D_5,
  output D_6,
  output D_7
);

  wire not_1_out, not_2_out, not_3_out;

  not not_1 (not_1_out, S_2);
  not not_2 (not_2_out, S_1);
  not not_3 (not_3_out, S_0);
  and and_1 (D_0, not_1_out, not_2_out, not_3_out, IN);
  and and_2 (D_1, not_1_out, not_2_out, S_0, IN);
  and and_3 (D_2, not_1_out, S_1, not_3_out, IN);
  and and_4 (D_3, not_1_out, S_1, S_0, IN);
  and and_5 (D_4, S_2, not_2_out, not_3_out, IN);
  and and_6 (D_5, S_2, not_2_out, S_0, IN);
  and and_7 (D_6, S_2, S_1, not_3_out, IN);
  and and_8 (D_7, S_2, S_1, S_0, IN);
endmodule
