// Digital circuit 2048_BIT_MEMORY.dig as structural Verilog
module _2048_BIT_MEMORY (
  input  [7:0] DATA_IN,
  input  READ_ENB,
  input  WR_ENB,
  input  [3:0] ROW_ADDR,
  input  [3:0] COL_ADDR,
  output [7:0] OUT
);

  _16x16_LATCH_MATRIX _16x16_latch_matrix_1 (
    .DATA_IN(DATA_IN[0]), .READ_ENB(READ_ENB), .WR_ENB(WR_ENB), .RS_3(ROW_ADDR[3]), .RS_2(ROW_ADDR[2]),
    .RS_1(ROW_ADDR[1]), .RS_0(ROW_ADDR[0]), .CS_3(COL_ADDR[3]), .CS_2(COL_ADDR[2]), .CS_1(COL_ADDR[1]),
    .CS_0(COL_ADDR[0]), .OUT(OUT[0]));
  _16x16_LATCH_MATRIX _16x16_latch_matrix_2 (
    .DATA_IN(DATA_IN[1]), .READ_ENB(READ_ENB), .WR_ENB(WR_ENB), .RS_3(ROW_ADDR[3]), .RS_2(ROW_ADDR[2]),
    .RS_1(ROW_ADDR[1]), .RS_0(ROW_ADDR[0]), .CS_3(COL_ADDR[3]), .CS_2(COL_ADDR[2]), .CS_1(COL_ADDR[1]),
    .CS_0(COL_ADDR[0]), .OUT(OUT[1]));
  _16x16_LATCH_MATRIX _16x16_latch_matrix_3 (
    .DATA_IN(DATA_IN[2]), .READ_ENB(READ_ENB), .WR_ENB(WR_ENB), .RS_3(ROW_ADDR[3]), .RS_2(ROW_ADDR[2]),
    .RS_1(ROW_ADDR[1]), .RS_0(ROW_ADDR[0]), .CS_3(COL_ADDR[3]), .CS_2(COL_ADDR[2]), .CS_1(COL_ADDR[1]),
    .CS_0(COL_ADDR[0]), .OUT(OUT[2]));
  _16x16_LATCH_MATRIX _16x16_latch_matrix_4 (
    .DATA_IN(DATA_IN[3]), .READ_ENB(READ_ENB), .WR_ENB(WR_ENB), .RS_3(ROW_ADDR[3]), .RS_2(ROW_ADDR[2]),
    .RS_1(ROW_ADDR[1]), .RS_0(ROW_ADDR[0]), .CS_3(COL_ADDR[3]), .CS_2(COL_ADDR[2]), .CS_1(COL_ADDR[1]),
    .CS_0(COL_ADDR[0]), .OUT(OUT[3]));
  _16x16_LATCH_MATRIX _16x16_latch_matrix_5 (
    .DATA_IN(DATA_IN[4]), .READ_ENB(READ_ENB), .WR_ENB(WR_ENB), .RS_3(ROW_ADDR[3]), .RS_2(ROW_ADDR[2]),
    .RS_1(ROW_ADDR[1]), .RS_0(ROW_ADDR[0]), .CS_3(COL_ADDR[3]), .CS_2(COL_ADDR[2]), .CS_1(COL_ADDR[1]),
    .CS_0(COL_ADDR[0]), .OUT(OUT[4]));
  _16x16_LATCH_MATRIX _16x16_latch_matrix_6 (
    .DATA_IN(DATA_IN[5]), .READ_ENB(READ_ENB), .WR_ENB(WR_ENB), .RS_3(ROW_ADDR[3]), .RS_2(ROW_ADDR[2]),
    .RS_1(ROW_ADDR[1]), .RS_0(ROW_ADDR[0]), .CS_3(COL_ADDR[3]), .CS_2(COL_ADDR[2]), .CS_1(COL_ADDR[1]),
    .CS_0(COL_ADDR[0]), .OUT(OUT[5]));
  _16x16_LATCH_MATRIX _16x16_latch_matrix_7 (
    .DATA_IN(DATA_IN[6]), .READ_ENB(READ_ENB), .WR_ENB(WR_ENB), .RS_3(ROW_ADDR[3]), .RS_2(ROW_ADDR[2]),
    .RS_1(ROW_ADDR[1]), .RS_0(ROW_ADDR[0]), .CS_3(COL_ADDR[3]), .CS_2(COL_ADDR[2]), .CS_1(COL_ADDR[1]),
    .CS_0(COL_ADDR[0]), .OUT(OUT[6]));
  _16x16_LATCH_MATRIX _16x16_latch_matrix_8 (
    .DATA_IN(DATA_IN[7]), .READ_ENB(READ_ENB), .WR_ENB(WR_ENB), .RS_3(ROW_ADDR[3]), .RS_2(ROW_ADDR[2]),
    .RS_1(ROW_ADDR[1]), .RS_0(ROW_ADDR[0]), .CS_3(COL_ADDR[3]), .CS_2(COL_ADDR[2]), .CS_1(COL_ADDR[1]),
    .CS_0(COL_ADDR[0]), .OUT(OUT[7]));
endmodule
