// Digital circuit 2X1_MULTIPLEXER.dig as structural Verilog
module _2X1_MULTIPLEXER (
  input  IN,
  input  S,
  output D_0,
  output D_1
);

  wire not_1_out;

  not not_1 (not_1_out, S);
  and and_1 (D_0, IN, not_1_out);
  and and_2 (D_1, IN, S);
endmodule
