// Digital circuit 2_BIT_MULTIPLIER.dig as structural Verilog
module _2_BIT_MULTIPLIER (
  input  [1:0] A,
  input  [1:0] B,
  output [3:0] A_B
);

  wire and_1_out, and_3_out, and_4_out, half_adder_2_sum;

  and and_1 (and_1_out, A[1], B[1]);
  and and_2 (A_B[0], A[0], B[0]);
  and and_3 (and_3_out, B[1], A[0]);
  and and_4 (and_4_out, A[1], B[0]);
  HALF_ADDER half_adder_1 (.A(half_adder_2_sum), .B(and_1_out), .SUM(A_B[3]), .CARRY(A_B[2]));
  HALF_ADDER half_adder_2 (.A(and_4_out), .B(and_3_out), .SUM(half_adder_2_sum), .CARRY(A_B[1]));
endmodule
