// Digital circuit 3X8_DECODER.dig as structural Verilog
module _3X8_DECODER (
  input  A,
  input  B,
  input  C,
  input  E,
  output D_0,
  output D_1,
  output D_2,
  output D_3,
  output D_4,
  output D_5,
  output D_6,
  output D_7
);

  wire not_1_out, not_2_out, not_3_out;

  not not_1 (not_1_out, A);
  not not_2 (not_2_out, B);
  not not_3 (not_3_out, C);
  and and_1 (D_0, not_1_out, not_2_out, not_3_out, E);
  and and_2 (D_1, not_1_out, not_2_out, C, E);
  and and_3 (D_2, not_1_out, B, not_3_out, E);
  and and_4 (D_3, not_1_out, B, C, E);
  and and_5 (D_4, A, not_2_out, not_3_out, E);
  and and_6 (D_5, A, not_2_out, C, E);
  and and_7 (D_6, A, B, not_3_out, E);
  and and_8 (D_7, A, B, C, E);
endmodule
