// Digital circuit 4X1_MTPLX_4_REGS.dig as structural Verilog
module _4X1_MTPLX_4_REGS (
  input  D_0,
  input  D_1,
  input  D_2,
  input  D_3,
  input  S_1,
  input  S_0,
  output Y
);

  wire and_1_out, and_2_out, and_3_out, and_4_out, not_1_out, not_2_out;

  not not_1 (not_1_out, S_0);
  not not_2 (not_2_out, S_1);
  and and_1 (and_1_out, not_1_out, not_2_out, D_0);
  and and_2 (and_2_out, S_0, not_2_out, D_1);
  and and_3 (and_3_out, not_1_out, S_1, D_2);
  and and_4 (and_4_out, S_0, S_1, D_3);
  or or_1 (Y, and_1_out, and_2_out, and_3_out, and_4_out);
endmodule
