// Digital circuit 4x4_LATCH_MATRIX.dig as structural Verilog
module _4x4_LATCH_MATRIX (
  input  IN,
  input  WR,
  input  READ,
  input  R_0,
  input  R_1,
  input  R_2,
  input  R_3,
  input  C_0,
  input  C_1,
  input  C_2,
  input  C_3,
  output OUT
);

  wire _4_bit_is_1_1_out, _4_bit_is_1_2_out, _4_bit_is_1_3_out, _4_bit_is_1_4_out, latch_matrix_unit_1_out,
       latch_matrix_unit_2_out, latch_matrix_unit_3_out, latch_matrix_unit_4_out, latch_matrix_unit_5_out,
       latch_matrix_unit_6_out, latch_matrix_unit_7_out, latch_matrix_unit_8_out, latch_matrix_unit_9_out,
       latch_matrix_unit_10_out, latch_matrix_unit_11_out, latch_matrix_unit_12_out,
       latch_matrix_unit_13_out, latch_matrix_unit_14_out, latch_matrix_unit_15_out, latch_matrix_unit_16_out;

  LATCH_MATRIX_UNIT latch_matrix_unit_1 (
    .ENB_ROW(R_0), .ENB_COL(C_0), .IN(IN), .WR(WR), .READ(READ), .OUT(latch_matrix_unit_1_out));
  LATCH_MATRIX_UNIT latch_matrix_unit_2 (
    .ENB_ROW(R_1), .ENB_COL(C_0), .IN(IN), .WR(WR), .READ(READ), .OUT(latch_matrix_unit_2_out));
  LATCH_MATRIX_UNIT latch_matrix_unit_3 (
    .ENB_ROW(R_2), .ENB_COL(C_0), .IN(IN), .WR(WR), .READ(READ), .OUT(latch_matrix_unit_3_out));
  LATCH_MATRIX_UNIT latch_matrix_unit_4 (
    .ENB_ROW(R_3), .ENB_COL(C_0), .IN(IN), .WR(WR), .READ(READ), .OUT(latch_matrix_unit_4_out));
  LATCH_MATRIX_UNIT latch_matrix_unit_5 (
    .ENB_ROW(R_0), .ENB_COL(C_1), .IN(IN), .WR(WR), .READ(READ), .OUT(latch_matrix_unit_5_out));
  LATCH_MATRIX_UNIT latch_matrix_unit_6 (
    .ENB_ROW(R_1), .ENB_COL(C_1), .IN(IN), .WR(WR), .READ(READ), .OUT(latch_matrix_unit_6_out));
  LATCH_MATRIX_UNIT latch_matrix_unit_7 (
    .ENB_ROW(R_2), .ENB_COL(C_1), .IN(IN), .WR(WR), .READ(READ), .OUT(latch_matrix_unit_7_out));
  LATCH_MATRIX_UNIT latch_matrix_unit_8 (
    .ENB_ROW(R_3), .ENB_COL(C_1), .IN(IN), .WR(WR), .READ(READ), .OUT(latch_matrix_unit_8_out));
  LATCH_MATRIX_UNIT latch_matrix_unit_9 (
    .ENB_ROW(R_0), .ENB_COL(C_2), .IN(IN), .WR(WR), .READ(READ), .OUT(latch_matrix_unit_9_out));
  LATCH_MATRIX_UNIT latch_matrix_unit_10 (
    .ENB_ROW(R_1), .ENB_COL(C_2), .IN(IN), .WR(WR), .READ(READ), .OUT(latch_matrix_unit_10_out));
  LATCH_MATRIX_UNIT latch_matrix_unit_11 (
    .ENB_ROW(R_2), .ENB_COL(C_2), .IN(IN), .WR(WR), .READ(READ), .OUT(latch_matrix_unit_11_out));
  LATCH_MATRIX_UNIT latch_matrix_unit_12 (
    .ENB_ROW(R_3), .ENB_COL(C_2), .IN(IN), .WR(WR), .READ(READ), .OUT(latch_matrix_unit_12_out));
  LATCH_MATRIX_UNIT latch_matrix_unit_13 (
    .ENB_ROW(R_0), .ENB_COL(C_3), .IN(IN), .WR(WR), .READ(READ), .OUT(latch_matrix_unit_13_out));
  LATCH_MATRIX_UNIT latch_matrix_unit_14 (
    .ENB_ROW(R_1), .ENB_COL(C_3), .IN(IN), .WR(WR), .READ(READ), .OUT(latch_matrix_unit_14_out));
  LATCH_MATRIX_UNIT latch_matrix_unit_15 (
    .ENB_ROW(R_2), .ENB_COL(C_3), .IN(IN), .WR(WR), .READ(READ), .OUT(latch_matrix_unit_15_out));
  LATCH_MATRIX_UNIT latch_matrix_unit_16 (
    .ENB_ROW(R_3), .ENB_COL(C_3), .IN(IN), .WR(WR), .READ(READ), .OUT(latch_matrix_unit_16_out));
  _4_BIT_IS_1 _4_bit_is_1_1 (
    .IN_0(latch_matrix_unit_1_out), .IN_1(latch_matrix_unit_5_out), .IN_2(latch_matrix_unit_9_out),
    .IN_3(latch_matrix_unit_13_out), .OUT(_4_bit_is_1_1_out));
  _4_BIT_IS_1 _4_bit_is_1_2 (
    .IN_0(latch_matrix_unit_2_out), .IN_1(latch_matrix_unit_6_out), .IN_2(latch_matrix_unit_10_out),
    .IN_3(latch_matrix_unit_14_out), .OUT(_4_bit_is_1_2_out));
  _4_BIT_IS_1 _4_bit_is_1_3 (
    .IN_0(latch_matrix_unit_3_out), .IN_1(latch_matrix_unit_7_out), .IN_2(latch_matrix_unit_11_out),
    .IN_3(latch_matrix_unit_15_out), .OUT(_4_bit_is_1_3_out));
  _4_BIT_IS_1 _4_bit_is_1_4 (
    .IN_0(latch_matrix_unit_4_out), .IN_1(latch_matrix_unit_8_out), .IN_2(latch_matrix_unit_12_out),
    .IN_3(latch_matrix_unit_16_out), .OUT(_4_bit_is_1_4_out));
  _4_BIT_IS_1 _4_bit_is_1_5 (
    .IN_0(_4_bit_is_1_1_out), .IN_1(_4_bit_is_1_2_out), .IN_2(_4_bit_is_1_3_out), .IN_3(_4_bit_is_1_4_out),
    .OUT(OUT));
endmodule
