// Digital circuit 8_BIT_AND.dig as structural Verilog
module _8_BIT_AND (
  input  [7:0] A,
  input  [7:0] B,
  output [7:0] A_B
);

  and and_1 (A_B[0], A[0], B[0]);
  and and_2 (A_B[1], A[1], B[1]);
  and and_3 (A_B[2], A[2], B[2]);
  and and_4 (A_B[3], A[3], B[3]);
  and and_5 (A_B[4], A[4], B[4]);
  and and_6 (A_B[5], A[5], B[5]);
  and and_7 (A_B[6], A[6], B[6]);
  and and_8 (A_B[7], A[7], B[7]);
endmodule
