// Digital circuit 8_BIT_BIDIRECTIONAL_SHIFT_REG.dig as structural Verilog
module _8_BIT_BIDIRECTIONAL_SHIFT_REG (
  input  IN_RS,
  input  R_L,
  input  CLK,
  input  CLEAR,
  input  IN_LS,
  output OUT_0,
  output OUT_1,
  output OUT_2,
  output OUT_3,
  output OUT_4,
  output OUT_5,
  output OUT_6,
  output OUT_7
);

  wire _2x1_mtplx_4_regs_1_y, _2x1_mtplx_4_regs_2_y, _2x1_mtplx_4_regs_3_y, _2x1_mtplx_4_regs_4_y,
       _2x1_mtplx_4_regs_5_y, _2x1_mtplx_4_regs_6_y, _2x1_mtplx_4_regs_7_y, _2x1_mtplx_4_regs_8_y, and_1_out,
       and_2_out, and_3_out, and_4_out, and_5_out, and_6_out, and_7_out, and_8_out, not_1_out;

  not not_1 (not_1_out, CLEAR);
  _2X1_MTPLX_4_REGS _2x1_mtplx_4_regs_1 (.SEL(R_L), .D_0(OUT_6), .D_1(IN_RS), .Y(_2x1_mtplx_4_regs_1_y));
  and and_1 (and_1_out, _2x1_mtplx_4_regs_1_y, not_1_out);
  MASTER_SLAVE_D_TYPE_FLIP_FLOP master_slave_d_type_flip_flop_1 (.DATA(and_1_out), .CLK(CLK), .Q(OUT_7));
  _2X1_MTPLX_4_REGS _2x1_mtplx_4_regs_2 (.SEL(R_L), .D_0(OUT_5), .D_1(OUT_7), .Y(_2x1_mtplx_4_regs_2_y));
  and and_2 (and_2_out, _2x1_mtplx_4_regs_2_y, not_1_out);
  MASTER_SLAVE_D_TYPE_FLIP_FLOP master_slave_d_type_flip_flop_2 (.DATA(and_2_out), .CLK(CLK), .Q(OUT_6));
  _2X1_MTPLX_4_REGS _2x1_mtplx_4_regs_3 (.SEL(R_L), .D_0(OUT_4), .D_1(OUT_6), .Y(_2x1_mtplx_4_regs_3_y));
  and and_3 (and_3_out, _2x1_mtplx_4_regs_3_y, not_1_out);
  MASTER_SLAVE_D_TYPE_FLIP_FLOP master_slave_d_type_flip_flop_3 (.DATA(and_3_out), .CLK(CLK), .Q(OUT_5));
  _2X1_MTPLX_4_REGS _2x1_mtplx_4_regs_4 (.SEL(R_L), .D_0(OUT_3), .D_1(OUT_5), .Y(_2x1_mtplx_4_regs_4_y));
  and and_4 (and_4_out, _2x1_mtplx_4_regs_4_y, not_1_out);
  MASTER_SLAVE_D_TYPE_FLIP_FLOP master_slave_d_type_flip_flop_4 (.DATA(and_4_out), .CLK(CLK), .Q(OUT_4));
  _2X1_MTPLX_4_REGS _2x1_mtplx_4_regs_5 (.SEL(R_L), .D_0(OUT_2), .D_1(OUT_4), .Y(_2x1_mtplx_4_regs_5_y));
  and and_5 (and_5_out, _2x1_mtplx_4_regs_5_y, not_1_out);
  MASTER_SLAVE_D_TYPE_FLIP_FLOP master_slave_d_type_flip_flop_5 (.DATA(and_5_out), .CLK(CLK), .Q(OUT_3));
  _2X1_MTPLX_4_REGS _2x1_mtplx_4_regs_6 (.SEL(R_L), .D_0(OUT_1), .D_1(OUT_3), .Y(_2x1_mtplx_4_regs_6_y));
  and and_6 (and_6_out, _2x1_mtplx_4_regs_6_y, not_1_out);
  MASTER_SLAVE_D_TYPE_FLIP_FLOP master_slave_d_type_flip_flop_6 (.DATA(and_6_out), .CLK(CLK), .Q(OUT_2));
  _2X1_MTPLX_4_REGS _2x1_mtplx_4_regs_7 (.SEL(R_L), .D_0(OUT_0), .D_1(OUT_2), .Y(_2x1_mtplx_4_regs_7_y));
  and and_7 (and_7_out, _2x1_mtplx_4_regs_7_y, not_1_out);
  MASTER_SLAVE_D_TYPE_FLIP_FLOP master_slave_d_type_flip_flop_7 (.DATA(and_7_out), .CLK(CLK), .Q(OUT_1));
  _2X1_MTPLX_4_REGS _2x1_mtplx_4_regs_8 (.SEL(R_L), .D_0(IN_LS), .D_1(OUT_1), .Y(_2x1_mtplx_4_regs_8_y));
  and and_8 (and_8_out, _2x1_mtplx_4_regs_8_y, not_1_out);
  MASTER_SLAVE_D_TYPE_FLIP_FLOP master_slave_d_type_flip_flop_8 (.DATA(and_8_out), .CLK(CLK), .Q(OUT_0));
endmodule
