// Digital circuit 8_BIT_IS_ZERO.dig as structural Verilog
module _8_BIT_IS_ZERO (
  input  [7:0] NUM,
  output IS_ZERO
);

  wire or_1_out, or_2_out, or_3_out, or_4_out, or_5_out, or_6_out, or_7_out;

  or or_1 (or_1_out, NUM[0], NUM[1]);
  or or_2 (or_2_out, NUM[2], NUM[3]);
  or or_3 (or_3_out, NUM[4], NUM[5]);
  or or_4 (or_4_out, NUM[6], NUM[7]);
  or or_5 (or_5_out, or_1_out, or_2_out);
  or or_6 (or_6_out, or_3_out, or_4_out);
  or or_7 (or_7_out, or_5_out, or_6_out);
  not not_1 (IS_ZERO, or_7_out);
endmodule
