// Digital circuit 8_BIT_PIPO_SHIFT_REG.dig as structural Verilog
module _8_BIT_PIPO_SHIFT_REG (
  input  IN_0,
  input  CLK,
  input  LOAD,
  input  CLEAR,
  input  IN_1,
  input  IN_2,
  input  IN_3,
  input  IN_4,
  input  IN_5,
  input  IN_6,
  input  IN_7,
  output OUT_0,
  output OUT_1,
  output OUT_2,
  output OUT_3,
  output OUT_4,
  output OUT_5,
  output OUT_6,
  output OUT_7
);

  wire and_1_out, and_2_out, and_3_out, and_4_out, and_5_out, and_6_out, and_7_out, and_8_out, and_9_out,
       and_10_out, and_11_out, and_12_out, and_13_out, and_14_out, and_15_out, and_16_out, and_17_out,
       and_18_out, and_19_out, and_20_out, and_21_out, and_22_out, and_23_out, and_24_out, not_1_out,
       not_2_out, or_1_out, or_2_out, or_3_out, or_4_out, or_5_out, or_6_out, or_7_out, or_8_out;

  not not_1 (not_1_out, LOAD);
  not not_2 (not_2_out, CLEAR);
  and and_1 (and_1_out, LOAD, IN_0);
  and and_2 (and_2_out, or_1_out, not_2_out);
  and and_3 (and_3_out, OUT_0, not_1_out);
  or or_1 (or_1_out, and_3_out, and_1_out);
  MASTER_SLAVE_D_TYPE_FLIP_FLOP master_slave_d_type_flip_flop_1 (.DATA(and_2_out), .CLK(CLK), .Q(OUT_0));
  and and_4 (and_4_out, LOAD, IN_1);
  and and_5 (and_5_out, or_2_out, not_2_out);
  and and_6 (and_6_out, OUT_1, not_1_out);
  or or_2 (or_2_out, and_6_out, and_4_out);
  MASTER_SLAVE_D_TYPE_FLIP_FLOP master_slave_d_type_flip_flop_2 (.DATA(and_5_out), .CLK(CLK), .Q(OUT_1));
  and and_7 (and_7_out, or_3_out, not_2_out);
  and and_8 (and_8_out, LOAD, IN_2);
  or or_3 (or_3_out, and_9_out, and_8_out);
  and and_9 (and_9_out, OUT_2, not_1_out);
  MASTER_SLAVE_D_TYPE_FLIP_FLOP master_slave_d_type_flip_flop_3 (.DATA(and_7_out), .CLK(CLK), .Q(OUT_2));
  and and_10 (and_10_out, LOAD, IN_3);
  and and_11 (and_11_out, or_4_out, not_2_out);
  or or_4 (or_4_out, and_12_out, and_10_out);
  MASTER_SLAVE_D_TYPE_FLIP_FLOP master_slave_d_type_flip_flop_4 (.DATA(and_11_out), .CLK(CLK), .Q(OUT_3));
  and and_12 (and_12_out, OUT_3, not_1_out);
  and and_13 (and_13_out, LOAD, IN_4);
  and and_14 (and_14_out, or_5_out, not_2_out);
  and and_15 (and_15_out, OUT_4, not_1_out);
  or or_5 (or_5_out, and_15_out, and_13_out);
  MASTER_SLAVE_D_TYPE_FLIP_FLOP master_slave_d_type_flip_flop_5 (.DATA(and_14_out), .CLK(CLK), .Q(OUT_4));
  and and_16 (and_16_out, LOAD, IN_5);
  and and_17 (and_17_out, or_6_out, not_2_out);
  and and_18 (and_18_out, OUT_5, not_1_out);
  or or_6 (or_6_out, and_18_out, and_16_out);
  MASTER_SLAVE_D_TYPE_FLIP_FLOP master_slave_d_type_flip_flop_6 (.DATA(and_17_out), .CLK(CLK), .Q(OUT_5));
  and and_19 (and_19_out, or_7_out, not_2_out);
  and and_20 (and_20_out, LOAD, IN_6);
  or or_7 (or_7_out, and_21_out, and_20_out);
  and and_21 (and_21_out, OUT_6, not_1_out);
  MASTER_SLAVE_D_TYPE_FLIP_FLOP master_slave_d_type_flip_flop_7 (.DATA(and_19_out), .CLK(CLK), .Q(OUT_6));
  and and_22 (and_22_out, LOAD, IN_7);
  and and_23 (and_23_out, or_8_out, not_2_out);
  or or_8 (or_8_out, and_24_out, and_22_out);
  MASTER_SLAVE_D_TYPE_FLIP_FLOP master_slave_d_type_flip_flop_8 (.DATA(and_23_out), .CLK(CLK), .Q(OUT_7));
  and and_24 (and_24_out, OUT_7, not_1_out);
endmodule
