// Digital circuit 8_BIT_PISO_SHIFT_REG.dig as structural Verilog
module _8_BIT_PISO_SHIFT_REG (
  input  LD_SH,
  input  IN_0,
  input  IN_1,
  input  SI,
  input  CLEAR,
  input  CLK,
  input  IN_2,
  input  IN_3,
  input  IN_4,
  input  IN_5,
  input  IN_7,
  input  IN_6,
  output SO
);

  wire _2x1_mtplx_4_regs_1_y, _2x1_mtplx_4_regs_2_y, _2x1_mtplx_4_regs_3_y, _2x1_mtplx_4_regs_4_y,
       _2x1_mtplx_4_regs_5_y, _2x1_mtplx_4_regs_6_y, _2x1_mtplx_4_regs_7_y, _2x1_mtplx_4_regs_8_y, and_1_out,
       and_2_out, and_3_out, and_4_out, and_5_out, and_6_out, and_7_out, and_8_out,
       master_slave_d_type_flip_flop_1_q, master_slave_d_type_flip_flop_2_q,
       master_slave_d_type_flip_flop_3_q, master_slave_d_type_flip_flop_4_q,
       master_slave_d_type_flip_flop_5_q, master_slave_d_type_flip_flop_6_q,
       master_slave_d_type_flip_flop_7_q, not_1_out;

  not not_1 (not_1_out, CLEAR);
  _2X1_MTPLX_4_REGS _2x1_mtplx_4_regs_1 (.SEL(LD_SH), .D_0(SI), .D_1(IN_7), .Y(_2x1_mtplx_4_regs_1_y));
  and and_1 (and_1_out, _2x1_mtplx_4_regs_1_y, not_1_out);
  MASTER_SLAVE_D_TYPE_FLIP_FLOP master_slave_d_type_flip_flop_1 (
    .DATA(and_1_out), .CLK(CLK), .Q(master_slave_d_type_flip_flop_1_q));
  _2X1_MTPLX_4_REGS _2x1_mtplx_4_regs_2 (
    .SEL(LD_SH), .D_0(master_slave_d_type_flip_flop_1_q), .D_1(IN_6), .Y(_2x1_mtplx_4_regs_2_y));
  and and_2 (and_2_out, _2x1_mtplx_4_regs_2_y, not_1_out);
  MASTER_SLAVE_D_TYPE_FLIP_FLOP master_slave_d_type_flip_flop_2 (
    .DATA(and_2_out), .CLK(CLK), .Q(master_slave_d_type_flip_flop_2_q));
  _2X1_MTPLX_4_REGS _2x1_mtplx_4_regs_3 (
    .SEL(LD_SH), .D_0(master_slave_d_type_flip_flop_2_q), .D_1(IN_5), .Y(_2x1_mtplx_4_regs_3_y));
  and and_3 (and_3_out, _2x1_mtplx_4_regs_3_y, not_1_out);
  MASTER_SLAVE_D_TYPE_FLIP_FLOP master_slave_d_type_flip_flop_3 (
    .DATA(and_3_out), .CLK(CLK), .Q(master_slave_d_type_flip_flop_3_q));
  _2X1_MTPLX_4_REGS _2x1_mtplx_4_regs_4 (
    .SEL(LD_SH), .D_0(master_slave_d_type_flip_flop_3_q), .D_1(IN_4), .Y(_2x1_mtplx_4_regs_4_y));
  and and_4 (and_4_out, _2x1_mtplx_4_regs_4_y, not_1_out);
  MASTER_SLAVE_D_TYPE_FLIP_FLOP master_slave_d_type_flip_flop_4 (
    .DATA(and_4_out), .CLK(CLK), .Q(master_slave_d_type_flip_flop_4_q));
  _2X1_MTPLX_4_REGS _2x1_mtplx_4_regs_5 (
    .SEL(LD_SH), .D_0(master_slave_d_type_flip_flop_4_q), .D_1(IN_3), .Y(_2x1_mtplx_4_regs_5_y));
  and and_5 (and_5_out, _2x1_mtplx_4_regs_5_y, not_1_out);
  MASTER_SLAVE_D_TYPE_FLIP_FLOP master_slave_d_type_flip_flop_5 (
    .DATA(and_5_out), .CLK(CLK), .Q(master_slave_d_type_flip_flop_5_q));
  _2X1_MTPLX_4_REGS _2x1_mtplx_4_regs_6 (
    .SEL(LD_SH), .D_0(master_slave_d_type_flip_flop_5_q), .D_1(IN_2), .Y(_2x1_mtplx_4_regs_6_y));
  and and_6 (and_6_out, _2x1_mtplx_4_regs_6_y, not_1_out);
  MASTER_SLAVE_D_TYPE_FLIP_FLOP master_slave_d_type_flip_flop_6 (
    .DATA(and_6_out), .CLK(CLK), .Q(master_slave_d_type_flip_flop_6_q));
  _2X1_MTPLX_4_REGS _2x1_mtplx_4_regs_7 (
    .SEL(LD_SH), .D_0(master_slave_d_type_flip_flop_6_q), .D_1(IN_1), .Y(_2x1_mtplx_4_regs_7_y));
  and and_7 (and_7_out, _2x1_mtplx_4_regs_7_y, not_1_out);
  MASTER_SLAVE_D_TYPE_FLIP_FLOP master_slave_d_type_flip_flop_7 (
    .DATA(and_7_out), .CLK(CLK), .Q(master_slave_d_type_flip_flop_7_q));
  _2X1_MTPLX_4_REGS _2x1_mtplx_4_regs_8 (
    .SEL(LD_SH), .D_0(master_slave_d_type_flip_flop_7_q), .D_1(IN_0), .Y(_2x1_mtplx_4_regs_8_y));
  and and_8 (and_8_out, _2x1_mtplx_4_regs_8_y, not_1_out);
  MASTER_SLAVE_D_TYPE_FLIP_FLOP master_slave_d_type_flip_flop_8 (.DATA(and_8_out), .CLK(CLK), .Q(SO));
endmodule
