// Digital circuit 8_BIT_SEQUENTIAL_SHIFT_AND_SUBTRACT_DIVIDER.dig as structural Verilog
module _8_BIT_SEQUENTIAL_SHIFT_AND_SUBTRACT_DIVIDER (
  input  [1:0] DIVIDEND
);

  wire pu_1_c_out, pu_1_y, pu_2_c_out, pu_2_y, pu_3_c_out, pu_4_c_out, pu_4_y, pu_5_c_out, pu_6_c_out,
       pu_7_c_out, pu_8_c_out, undriven, undriven_2, undriven_3, undriven_4;

  PU pu_1 (.B(DIVIDEND[1]), .A(1'b0), .C_OUT(pu_1_c_out), .SEL(pu_1_c_out), .Y(pu_1_y), .C_IN(pu_4_c_out));
  PU pu_2 (.B(pu_1_y), .A(pu_4_y), .C_OUT(pu_2_c_out), .SEL(pu_2_c_out), .Y(pu_2_y), .C_IN(pu_6_c_out));
  PU pu_3 (.B(1'b0), .A(pu_2_y), .C_OUT(pu_3_c_out), .SEL(pu_3_c_out), .C_IN(pu_7_c_out));  // open: Y
  PU pu_4 (.B(DIVIDEND[0]), .A(undriven), .C_OUT(pu_4_c_out), .SEL(pu_1_c_out), .Y(pu_4_y), .C_IN(1'b1));
  PU pu_5 (.C_OUT(pu_5_c_out), .SEL(pu_5_c_out), .C_IN(pu_8_c_out));  // open: B, A, Y
  PU pu_6 (.B(pu_4_y), .A(undriven_2), .C_OUT(pu_6_c_out), .SEL(pu_2_c_out), .C_IN(1'b1));  // open: Y
  PU pu_7 (.B(pu_2_y), .A(undriven_3), .C_OUT(pu_7_c_out), .SEL(pu_3_c_out), .C_IN(1'b1));  // open: Y
  PU pu_8 (.A(undriven_4), .C_OUT(pu_8_c_out), .SEL(pu_5_c_out), .C_IN(1'b1));  // open: B, Y
  // Pins of 1 and 2 bits meet at DIVIDEND
endmodule
