// Digital circuit 8_BIT_SHIFT_DIVIDER.dig as structural Verilog
module _8_BIT_SHIFT_DIVIDER (
  input  in_1
);

  _8_BIT_UNIVERSAL_SHIFT_REG _8_bit_universal_shift_reg_1 ();  // open: IN_0, IN_1, IN_2, IN_3, IN_4, IN_5, IN_6, IN_7, S_0, S_1, SI_LEFTSHIFT, SI_RIGHT_SHIFT, CLK, CLEAR, OUT_0, OUT_1, OUT_2, OUT_3, OUT_4, OUT_5, OUT_6, OUT_7
endmodule
