// Digital circuit 8_BIT_SIPO_SHIFT_REG.dig as structural Verilog
module _8_BIT_SIPO_SHIFT_REG (
  input  DATA,
  input  CLK,
  output Q_0,
  output Q_1,
  output Q_2,
  output Q_3,
  output Q_4,
  output Q_5,
  output Q_6,
  output Q_7
);

  MASTER_SLAVE_D_TYPE_FLIP_FLOP master_slave_d_type_flip_flop_1 (.DATA(DATA), .CLK(CLK), .Q(Q_0));
  MASTER_SLAVE_D_TYPE_FLIP_FLOP master_slave_d_type_flip_flop_2 (.DATA(Q_0), .CLK(CLK), .Q(Q_1));
  MASTER_SLAVE_D_TYPE_FLIP_FLOP master_slave_d_type_flip_flop_3 (.DATA(Q_1), .CLK(CLK), .Q(Q_2));
  MASTER_SLAVE_D_TYPE_FLIP_FLOP master_slave_d_type_flip_flop_4 (.DATA(Q_2), .CLK(CLK), .Q(Q_3));
  MASTER_SLAVE_D_TYPE_FLIP_FLOP master_slave_d_type_flip_flop_5 (.DATA(Q_3), .CLK(CLK), .Q(Q_4));
  MASTER_SLAVE_D_TYPE_FLIP_FLOP master_slave_d_type_flip_flop_6 (.DATA(Q_4), .CLK(CLK), .Q(Q_5));
  MASTER_SLAVE_D_TYPE_FLIP_FLOP master_slave_d_type_flip_flop_7 (.DATA(Q_5), .CLK(CLK), .Q(Q_6));
  MASTER_SLAVE_D_TYPE_FLIP_FLOP master_slave_d_type_flip_flop_8 (.DATA(Q_6), .CLK(CLK), .Q(Q_7));
endmodule
