// Digital circuit 8_BIT_SIPO_SHIFT_REG_WITH_INTERMEDIATE_REG.dig as structural Verilog
module _8_BIT_SIPO_SHIFT_REG_WITH_INTERMEDIATE_REG (
  input  DATA,
  input  CLK,
  input  CLK_2,
  input  CLEAR,
  output OUT_0,
  output OUT_1,
  output OUT_2,
  output OUT_3,
  output OUT_4,
  output OUT_5,
  output OUT_6,
  output OUT_7
);

  wire and_1_out, and_2_out, and_3_out, and_4_out, and_5_out, and_6_out, and_7_out, and_8_out,
       master_slave_d_type_flip_flop_1_q, master_slave_d_type_flip_flop_3_q,
       master_slave_d_type_flip_flop_5_q, master_slave_d_type_flip_flop_7_q,
       master_slave_d_type_flip_flop_9_q, master_slave_d_type_flip_flop_11_q,
       master_slave_d_type_flip_flop_13_q, master_slave_d_type_flip_flop_15_q, not_1_out;

  not not_1 (not_1_out, CLEAR);
  and and_1 (and_1_out, DATA, not_1_out);
  MASTER_SLAVE_D_TYPE_FLIP_FLOP master_slave_d_type_flip_flop_1 (
    .DATA(and_1_out), .CLK(CLK), .Q(master_slave_d_type_flip_flop_1_q));
  MASTER_SLAVE_D_TYPE_FLIP_FLOP master_slave_d_type_flip_flop_2 (
    .DATA(master_slave_d_type_flip_flop_1_q), .CLK(CLK_2), .Q(OUT_0));
  and and_2 (and_2_out, master_slave_d_type_flip_flop_1_q, not_1_out);
  MASTER_SLAVE_D_TYPE_FLIP_FLOP master_slave_d_type_flip_flop_3 (
    .DATA(and_2_out), .CLK(CLK), .Q(master_slave_d_type_flip_flop_3_q));
  MASTER_SLAVE_D_TYPE_FLIP_FLOP master_slave_d_type_flip_flop_4 (
    .DATA(master_slave_d_type_flip_flop_3_q), .CLK(CLK_2), .Q(OUT_1));
  and and_3 (and_3_out, master_slave_d_type_flip_flop_3_q, not_1_out);
  MASTER_SLAVE_D_TYPE_FLIP_FLOP master_slave_d_type_flip_flop_5 (
    .DATA(and_3_out), .CLK(CLK), .Q(master_slave_d_type_flip_flop_5_q));
  MASTER_SLAVE_D_TYPE_FLIP_FLOP master_slave_d_type_flip_flop_6 (
    .DATA(master_slave_d_type_flip_flop_5_q), .CLK(CLK_2), .Q(OUT_2));
  and and_4 (and_4_out, master_slave_d_type_flip_flop_5_q, not_1_out);
  MASTER_SLAVE_D_TYPE_FLIP_FLOP master_slave_d_type_flip_flop_7 (
    .DATA(and_4_out), .CLK(CLK), .Q(master_slave_d_type_flip_flop_7_q));
  MASTER_SLAVE_D_TYPE_FLIP_FLOP master_slave_d_type_flip_flop_8 (
    .DATA(master_slave_d_type_flip_flop_7_q), .CLK(CLK_2), .Q(OUT_3));
  and and_5 (and_5_out, master_slave_d_type_flip_flop_7_q, not_1_out);
  MASTER_SLAVE_D_TYPE_FLIP_FLOP master_slave_d_type_flip_flop_9 (
    .DATA(and_5_out), .CLK(CLK), .Q(master_slave_d_type_flip_flop_9_q));
  MASTER_SLAVE_D_TYPE_FLIP_FLOP master_slave_d_type_flip_flop_10 (
    .DATA(master_slave_d_type_flip_flop_9_q), .CLK(CLK_2), .Q(OUT_4));
  and and_6 (and_6_out, master_slave_d_type_flip_flop_9_q, not_1_out);
  MASTER_SLAVE_D_TYPE_FLIP_FLOP master_slave_d_type_flip_flop_11 (
    .DATA(and_6_out), .CLK(CLK), .Q(master_slave_d_type_flip_flop_11_q));
  MASTER_SLAVE_D_TYPE_FLIP_FLOP master_slave_d_type_flip_flop_12 (
    .DATA(master_slave_d_type_flip_flop_11_q), .CLK(CLK_2), .Q(OUT_5));
  and and_7 (and_7_out, master_slave_d_type_flip_flop_11_q, not_1_out);
  MASTER_SLAVE_D_TYPE_FLIP_FLOP master_slave_d_type_flip_flop_13 (
    .DATA(and_7_out), .CLK(CLK), .Q(master_slave_d_type_flip_flop_13_q));
  MASTER_SLAVE_D_TYPE_FLIP_FLOP master_slave_d_type_flip_flop_14 (
    .DATA(master_slave_d_type_flip_flop_13_q), .CLK(CLK_2), .Q(OUT_6));
  and and_8 (and_8_out, master_slave_d_type_flip_flop_13_q, not_1_out);
  MASTER_SLAVE_D_TYPE_FLIP_FLOP master_slave_d_type_flip_flop_15 (
    .DATA(and_8_out), .CLK(CLK), .Q(master_slave_d_type_flip_flop_15_q));
  MASTER_SLAVE_D_TYPE_FLIP_FLOP master_slave_d_type_flip_flop_16 (
    .DATA(master_slave_d_type_flip_flop_15_q), .CLK(CLK_2), .Q(OUT_7));
endmodule
