// Digital circuit 8_BIT_SISO_SHIFT_REG.dig as structural Verilog
module _8_BIT_SISO_SHIFT_REG (
  input  [7:0] DATA,
  input  CLK,
  input  LOAD
);

  wire and_1_out, and_2_out, and_3_out, and_4_out, and_5_out, and_6_out, and_7_out, and_8_out, and_9_out,
       and_10_out, and_11_out, and_12_out, and_13_out, and_14_out, and_15_out, and_16_out,
       master_slave_d_type_flip_flop_1_q, master_slave_d_type_flip_flop_2_q,
       master_slave_d_type_flip_flop_3_q, master_slave_d_type_flip_flop_4_q,
       master_slave_d_type_flip_flop_5_q, master_slave_d_type_flip_flop_6_q,
       master_slave_d_type_flip_flop_7_q, master_slave_d_type_flip_flop_8_q, not_1_out, or_1_out, or_2_out,
       or_3_out, or_4_out, or_5_out, or_6_out, or_7_out, or_8_out;

  not not_1 (not_1_out, LOAD);
  and and_1 (and_1_out, LOAD, DATA[0]);
  and and_2 (and_2_out, master_slave_d_type_flip_flop_1_q, not_1_out);
  or or_1 (or_1_out, and_2_out, and_1_out);
  MASTER_SLAVE_D_TYPE_FLIP_FLOP master_slave_d_type_flip_flop_1 (
    .DATA(or_1_out), .CLK(CLK), .Q(master_slave_d_type_flip_flop_1_q));
  and and_3 (and_3_out, LOAD, master_slave_d_type_flip_flop_1_q);
  or or_2 (or_2_out, and_4_out, and_3_out);
  and and_4 (and_4_out, master_slave_d_type_flip_flop_2_q, not_1_out);
  MASTER_SLAVE_D_TYPE_FLIP_FLOP master_slave_d_type_flip_flop_2 (
    .DATA(or_2_out), .CLK(CLK), .Q(master_slave_d_type_flip_flop_2_q));
  and and_5 (and_5_out, LOAD, master_slave_d_type_flip_flop_2_q);
  or or_3 (or_3_out, and_6_out, and_5_out);
  MASTER_SLAVE_D_TYPE_FLIP_FLOP master_slave_d_type_flip_flop_3 (
    .DATA(or_3_out), .CLK(CLK), .Q(master_slave_d_type_flip_flop_3_q));
  and and_6 (and_6_out, master_slave_d_type_flip_flop_3_q, not_1_out);
  and and_7 (and_7_out, LOAD, master_slave_d_type_flip_flop_3_q);
  and and_8 (and_8_out, master_slave_d_type_flip_flop_4_q, not_1_out);
  or or_4 (or_4_out, and_8_out, and_7_out);
  MASTER_SLAVE_D_TYPE_FLIP_FLOP master_slave_d_type_flip_flop_4 (
    .DATA(or_4_out), .CLK(CLK), .Q(master_slave_d_type_flip_flop_4_q));
  and and_9 (and_9_out, LOAD, master_slave_d_type_flip_flop_4_q);
  and and_10 (and_10_out, master_slave_d_type_flip_flop_5_q, not_1_out);
  or or_5 (or_5_out, and_10_out, and_9_out);
  MASTER_SLAVE_D_TYPE_FLIP_FLOP master_slave_d_type_flip_flop_5 (
    .DATA(or_5_out), .CLK(CLK), .Q(master_slave_d_type_flip_flop_5_q));
  and and_11 (and_11_out, LOAD, master_slave_d_type_flip_flop_5_q);
  or or_6 (or_6_out, and_12_out, and_11_out);
  and and_12 (and_12_out, master_slave_d_type_flip_flop_6_q, not_1_out);
  MASTER_SLAVE_D_TYPE_FLIP_FLOP master_slave_d_type_flip_flop_6 (
    .DATA(or_6_out), .CLK(CLK), .Q(master_slave_d_type_flip_flop_6_q));
  and and_13 (and_13_out, LOAD, master_slave_d_type_flip_flop_6_q);
  or or_7 (or_7_out, and_14_out, and_13_out);
  MASTER_SLAVE_D_TYPE_FLIP_FLOP master_slave_d_type_flip_flop_7 (
    .DATA(or_7_out), .CLK(CLK), .Q(master_slave_d_type_flip_flop_7_q));
  and and_14 (and_14_out, master_slave_d_type_flip_flop_7_q, not_1_out);
  and and_15 (and_15_out, LOAD, master_slave_d_type_flip_flop_7_q);
  and and_16 (and_16_out, master_slave_d_type_flip_flop_8_q, not_1_out);
  or or_8 (or_8_out, and_16_out, and_15_out);
  MASTER_SLAVE_D_TYPE_FLIP_FLOP master_slave_d_type_flip_flop_8 (
    .DATA(or_8_out), .CLK(CLK), .Q(master_slave_d_type_flip_flop_8_q));
  // Pins of 1 and 8 bits meet at DATA
endmodule
