// Digital circuit 8_BIT_SISO_SHIFT_REG_WITH_MTPLX.dig as structural Verilog
module _8_BIT_SISO_SHIFT_REG_WITH_MTPLX (
  input  DATA,
  input  CLK,
  input  LOAD,
  output OUT
);

  wire _2x1_mtplx_4_regs_1_y, _2x1_mtplx_4_regs_2_y, _2x1_mtplx_4_regs_3_y, _2x1_mtplx_4_regs_4_y,
       _2x1_mtplx_4_regs_5_y, _2x1_mtplx_4_regs_6_y, _2x1_mtplx_4_regs_7_y, _2x1_mtplx_4_regs_8_y,
       master_slave_d_type_flip_flop_1_q, master_slave_d_type_flip_flop_2_q,
       master_slave_d_type_flip_flop_3_q, master_slave_d_type_flip_flop_4_q,
       master_slave_d_type_flip_flop_5_q, master_slave_d_type_flip_flop_6_q,
       master_slave_d_type_flip_flop_7_q;

  _2X1_MTPLX_4_REGS _2x1_mtplx_4_regs_1 (
    .SEL(LOAD), .D_0(master_slave_d_type_flip_flop_1_q), .D_1(DATA), .Y(_2x1_mtplx_4_regs_1_y));
  MASTER_SLAVE_D_TYPE_FLIP_FLOP master_slave_d_type_flip_flop_1 (
    .DATA(_2x1_mtplx_4_regs_1_y), .CLK(CLK), .Q(master_slave_d_type_flip_flop_1_q));
  _2X1_MTPLX_4_REGS _2x1_mtplx_4_regs_2 (
    .SEL(LOAD), .D_0(master_slave_d_type_flip_flop_2_q), .D_1(master_slave_d_type_flip_flop_1_q),
    .Y(_2x1_mtplx_4_regs_2_y));
  MASTER_SLAVE_D_TYPE_FLIP_FLOP master_slave_d_type_flip_flop_2 (
    .DATA(_2x1_mtplx_4_regs_2_y), .CLK(CLK), .Q(master_slave_d_type_flip_flop_2_q));
  _2X1_MTPLX_4_REGS _2x1_mtplx_4_regs_3 (
    .SEL(LOAD), .D_0(master_slave_d_type_flip_flop_3_q), .D_1(master_slave_d_type_flip_flop_2_q),
    .Y(_2x1_mtplx_4_regs_3_y));
  MASTER_SLAVE_D_TYPE_FLIP_FLOP master_slave_d_type_flip_flop_3 (
    .DATA(_2x1_mtplx_4_regs_3_y), .CLK(CLK), .Q(master_slave_d_type_flip_flop_3_q));
  _2X1_MTPLX_4_REGS _2x1_mtplx_4_regs_4 (
    .SEL(LOAD), .D_0(master_slave_d_type_flip_flop_4_q), .D_1(master_slave_d_type_flip_flop_3_q),
    .Y(_2x1_mtplx_4_regs_4_y));
  MASTER_SLAVE_D_TYPE_FLIP_FLOP master_slave_d_type_flip_flop_4 (
    .DATA(_2x1_mtplx_4_regs_4_y), .CLK(CLK), .Q(master_slave_d_type_flip_flop_4_q));
  _2X1_MTPLX_4_REGS _2x1_mtplx_4_regs_5 (
    .SEL(LOAD), .D_0(master_slave_d_type_flip_flop_5_q), .D_1(master_slave_d_type_flip_flop_4_q),
    .Y(_2x1_mtplx_4_regs_5_y));
  MASTER_SLAVE_D_TYPE_FLIP_FLOP master_slave_d_type_flip_flop_5 (
    .DATA(_2x1_mtplx_4_regs_5_y), .CLK(CLK), .Q(master_slave_d_type_flip_flop_5_q));
  _2X1_MTPLX_4_REGS _2x1_mtplx_4_regs_6 (
    .SEL(LOAD), .D_0(master_slave_d_type_flip_flop_6_q), .D_1(master_slave_d_type_flip_flop_5_q),
    .Y(_2x1_mtplx_4_regs_6_y));
  MASTER_SLAVE_D_TYPE_FLIP_FLOP master_slave_d_type_flip_flop_6 (
    .DATA(_2x1_mtplx_4_regs_6_y), .CLK(CLK), .Q(master_slave_d_type_flip_flop_6_q));
  _2X1_MTPLX_4_REGS _2x1_mtplx_4_regs_7 (
    .SEL(LOAD), .D_0(master_slave_d_type_flip_flop_7_q), .D_1(master_slave_d_type_flip_flop_6_q),
    .Y(_2x1_mtplx_4_regs_7_y));
  MASTER_SLAVE_D_TYPE_FLIP_FLOP master_slave_d_type_flip_flop_7 (
    .DATA(_2x1_mtplx_4_regs_7_y), .CLK(CLK), .Q(master_slave_d_type_flip_flop_7_q));
  _2X1_MTPLX_4_REGS _2x1_mtplx_4_regs_8 (
    .SEL(LOAD), .D_0(OUT), .D_1(master_slave_d_type_flip_flop_7_q), .Y(_2x1_mtplx_4_regs_8_y));
  MASTER_SLAVE_D_TYPE_FLIP_FLOP master_slave_d_type_flip_flop_8 (.DATA(_2x1_mtplx_4_regs_8_y), .CLK(CLK), .Q(OUT));
endmodule
