// Digital circuit 8_BIT_UNIVERSAL_SHIFT_REG.dig as structural Verilog
module _8_BIT_UNIVERSAL_SHIFT_REG (
  input  IN_0,
  input  IN_1,
  input  IN_2,
  input  IN_3,
  input  IN_4,
  input  IN_5,
  input  IN_6,
  input  IN_7,
  input  S_0,
  input  S_1,
  input  SI_LEFTSHIFT,
  input  SI_RIGHT_SHIFT,
  input  CLK,
  input  CLEAR,
  output OUT_0,
  output OUT_1,
  output OUT_2,
  output OUT_3,
  output OUT_4,
  output OUT_5,
  output OUT_6,
  output OUT_7
);

  wire not_1_out;

  not not_1 (not_1_out, CLEAR);
  USR_RIGHT_SHIFT_UNIT usr_right_shift_unit_1 (
    .D_0(OUT_7), .D_2(OUT_6), .SI_RIGHT_SHIFT(SI_RIGHT_SHIFT), .S_1(S_1), .S_0(S_0), .CLEAR(not_1_out),
    .CLK(CLK), .Q(OUT_7), .D_3(IN_7));
  USR_UNIT usr_unit_1 (
    .D_0(OUT_6), .D_1(OUT_7), .D_2(OUT_5), .S_1(S_1), .S_0(S_0), .CLEAR(not_1_out), .CLK(CLK), .D_3(IN_6),
    .Q(OUT_6));
  USR_UNIT usr_unit_2 (
    .D_0(OUT_5), .D_1(OUT_6), .D_2(OUT_4), .S_1(S_1), .S_0(S_0), .CLEAR(not_1_out), .CLK(CLK), .D_3(IN_5),
    .Q(OUT_5));
  USR_UNIT usr_unit_3 (
    .D_0(OUT_4), .D_1(OUT_5), .D_2(OUT_3), .S_1(S_1), .S_0(S_0), .CLEAR(not_1_out), .CLK(CLK), .D_3(IN_4),
    .Q(OUT_4));
  USR_UNIT usr_unit_4 (
    .D_0(OUT_3), .D_1(OUT_4), .D_2(OUT_2), .S_1(S_1), .S_0(S_0), .CLEAR(not_1_out), .CLK(CLK), .D_3(IN_3),
    .Q(OUT_3));
  USR_UNIT usr_unit_5 (
    .D_0(OUT_2), .D_1(OUT_3), .D_2(OUT_1), .S_1(S_1), .S_0(S_0), .CLEAR(not_1_out), .CLK(CLK), .D_3(IN_2),
    .Q(OUT_2));
  USR_UNIT usr_unit_6 (
    .D_0(OUT_1), .D_1(OUT_2), .D_2(OUT_0), .S_1(S_1), .S_0(S_0), .CLEAR(not_1_out), .CLK(CLK), .D_3(IN_1),
    .Q(OUT_1));
  USR_LEFT_SHIFT_UNIT usr_left_shift_unit_1 (
    .D_0(OUT_0), .D_1(OUT_1), .SI_LEFT_SHIFT(SI_LEFTSHIFT), .S_1(S_1), .S_0(S_0), .CLEAR(not_1_out),
    .CLK(CLK), .Q(OUT_0), .D_3(IN_0));

  // Notes on the sheet:
  //   S1|SO|Function
  //   _________________
  //   0 | 0 | Hold
  //   0 | 1 | Shift right
  //   1 | 0 | Shift left
  //   1| 1 | Parallel load
endmodule
