// Digital circuit DFF_2.dig as structural Verilog
module DFF_2 (
  input  IN,
  input  CLK,
  output Q,
  output Q_2
);

  wire nand_1_out, nand_2_out, not_1_out;

  not not_1 (not_1_out, IN);
  nand nand_1 (nand_1_out, IN, CLK);
  nand nand_2 (nand_2_out, CLK, not_1_out);
  nand nand_3 (Q, nand_1_out, Q_2);
  nand nand_4 (Q_2, Q, nand_2_out);
endmodule
