// Digital circuit D_FLIP_FLOP.dig as structural Verilog
module D_FLIP_FLOP (
  input  D,
  input  CLK,
  output Q,
  output Q_2
);

  wire not_1_out;

  SR_FLIP_FLOP sr_flip_flop_1 (.S(D), .CLK(CLK), .R(not_1_out), .Q(Q), .Q_2(Q_2));
  not not_1 (not_1_out, D);
endmodule
