// Digital circuit D_TYPE_FLIP_FLOP_WITH_ASYNCHRONOUS_RESET.dig as structural Verilog
module D_TYPE_FLIP_FLOP_WITH_ASYNCHRONOUS_RESET (
  input  CLK,
  input  DATA,
  input  RESET,
  output Q,
  output NOT_Q
);

  wire nand_1_out, nand_2_out, nand_3_out, nand_4_out;

  nand nand_1 (nand_1_out, nand_4_out, nand_2_out);
  nand nand_2 (nand_2_out, nand_1_out, CLK, RESET);
  nand nand_3 (nand_3_out, nand_2_out, CLK, nand_4_out);
  nand nand_4 (nand_4_out, nand_3_out, DATA, RESET);
  nand nand_5 (Q, nand_2_out, NOT_Q);
  nand nand_6 (NOT_Q, Q, nand_3_out, RESET);
endmodule
