// Digital circuit FULL_SUBTRACTOR.dig as structural Verilog
module FULL_SUBTRACTOR (
  input  B_IN,
  input  A,
  input  B,
  output B_OUT,
  output DIFF
);

  wire half_subtractor_1_borrow, half_subtractor_1_difference, half_subtractor_2_borrow;

  HALF_SUBTRACTOR half_subtractor_1 (
    .A(A), .B(B), .DIFFERENCE(half_subtractor_1_difference), .BORROW(half_subtractor_1_borrow));
  HALF_SUBTRACTOR half_subtractor_2 (
    .A(half_subtractor_1_difference), .B(B_IN), .DIFFERENCE(DIFF), .BORROW(half_subtractor_2_borrow));
  or or_1 (B_OUT, half_subtractor_2_borrow, half_subtractor_1_borrow);
endmodule
