// Digital circuit HALF_SUBTRACTOR.dig as structural Verilog
module HALF_SUBTRACTOR (
  input  A,
  input  B,
  output DIFFERENCE,
  output BORROW
);

  wire not_1_out;

  not not_1 (not_1_out, A);
  xor xor_1 (DIFFERENCE, A, B);
  and and_1 (BORROW, B, not_1_out);
endmodule
