// Digital circuit JOHNSON.dig as structural Verilog
module JOHNSON (
  input  CLK,
  output Q_A,
  output Q_B,
  output Q_C,
  output Q_D
);

  wire dff_2_4_q_2;

  DFF_2 dff_2_1 (.IN(dff_2_4_q_2), .CLK(CLK), .Q(Q_A));  // open: Q_2
  DFF_2 dff_2_2 (.IN(Q_A), .CLK(CLK), .Q(Q_B));  // open: Q_2
  DFF_2 dff_2_3 (.IN(Q_B), .CLK(CLK), .Q(Q_C));  // open: Q_2
  DFF_2 dff_2_4 (.IN(Q_C), .CLK(CLK), .Q(Q_D), .Q_2(dff_2_4_q_2));
endmodule
