// Digital circuit LATCH_MATRIX_UNIT.dig as structural Verilog
module LATCH_MATRIX_UNIT (
  input  ENB_ROW,
  input  ENB_COL,
  input  IN,
  input  WR,
  input  READ,
  output OUT
);

  wire and_1_out, and_2_out, and_3_out, gated_sr_1_out;

  and and_1 (and_1_out, ENB_COL, ENB_ROW);
  and and_2 (and_2_out, WR, and_1_out);
  and and_3 (and_3_out, READ, and_1_out);
  GATED_SR gated_sr_1 (.WR(and_2_out), .IN(IN), .OUT(gated_sr_1_out));
  and and_4 (OUT, gated_sr_1_out, and_3_out);
endmodule
