// Digital circuit MASTER_SLAVE_D_TYPE_FLIP_FLOP.dig as structural Verilog
module MASTER_SLAVE_D_TYPE_FLIP_FLOP (
  input  DATA,
  input  CLK,
  output Q
);

  wire nand_1_out, nand_2_out, nand_3_out, nand_4_out, nand_5_out, nand_6_out, nand_8_out, not_1_out,
       not_2_out;

  not not_1 (not_1_out, DATA);
  nand nand_1 (nand_1_out, DATA, CLK);
  nand nand_2 (nand_2_out, CLK, not_1_out);
  nand nand_3 (nand_3_out, nand_1_out, nand_4_out);
  nand nand_4 (nand_4_out, nand_3_out, nand_2_out);
  not not_2 (not_2_out, CLK);
  nand nand_5 (nand_5_out, nand_3_out, not_2_out);
  nand nand_6 (nand_6_out, not_2_out, nand_4_out);
  nand nand_7 (Q, nand_5_out, nand_8_out);
  nand nand_8 (nand_8_out, Q, nand_6_out);

  // Notes on the sheet:
  //   Master D Flip-Flop
  //   SET
  //   RESET
  //   Slave SR Flip-FLop
endmodule
