// Digital circuit MODULAR_16X16LATCH_MATRIX.dig as structural Verilog
module MODULAR_16X16LATCH_MATRIX (
  input  R_0,
  input  R_1,
  input  R_2,
  input  R_3,
  input  R_4,
  input  R_5,
  input  R_6,
  input  R_7,
  input  R_8,
  input  R_9,
  input  R_10,
  input  R_11,
  input  R_12,
  input  R_13,
  input  R_14,
  input  R_15,
  input  WR,
  input  READ,
  input  IN,
  input  C_0,
  input  C_1,
  input  C_2,
  input  C_3,
  input  C_4,
  input  C_5,
  input  C_6,
  input  C_7,
  input  C_8,
  input  C_9,
  input  C_10,
  input  C_11,
  input  C_12,
  input  C_13,
  input  C_14,
  input  C_15,
  output OUT
);

  wire _4x16_latch_matrix_1_out, _4x16_latch_matrix_2_out, _4x16_latch_matrix_3_out, _4x16_latch_matrix_4_out;

  _4X16_LATCH_MATRIX _4x16_latch_matrix_1 (
    .IN(IN), .READ(READ), .WR(WR), .R_0(R_0), .R_1(R_1), .R_2(R_2), .R_3(R_3), .R_4(R_4), .R_5(R_5),
    .R_6(R_6), .R_7(R_7), .R_8(R_8), .R_9(R_9), .R_10(R_10), .R_11(R_11), .R_12(R_12), .R_13(R_13),
    .R_14(R_14), .R_15(R_15), .C_0(C_0), .C_1(C_1), .C_2(C_2), .C_3(C_3), .OUT(_4x16_latch_matrix_1_out));
  _4X16_LATCH_MATRIX _4x16_latch_matrix_2 (
    .IN(IN), .READ(READ), .WR(WR), .R_0(R_0), .R_1(R_1), .R_2(R_2), .R_3(R_3), .R_4(R_4), .R_5(R_5),
    .R_6(R_6), .R_7(R_7), .R_8(R_8), .R_9(R_9), .R_10(R_10), .R_11(R_11), .R_12(R_12), .R_13(R_13),
    .R_14(R_14), .R_15(R_15), .C_0(C_4), .C_1(C_5), .C_2(C_6), .C_3(C_7), .OUT(_4x16_latch_matrix_2_out));
  _4X16_LATCH_MATRIX _4x16_latch_matrix_3 (
    .IN(IN), .READ(READ), .WR(WR), .R_0(R_0), .R_1(R_1), .R_2(R_2), .R_3(R_3), .R_4(R_4), .R_5(R_5),
    .R_6(R_6), .R_7(R_7), .R_8(R_8), .R_9(R_9), .R_10(R_10), .R_11(R_11), .R_12(R_12), .R_13(R_13),
    .R_14(R_14), .R_15(R_15), .C_0(C_8), .C_1(C_9), .C_2(C_10), .C_3(C_11), .OUT(_4x16_latch_matrix_3_out));
  _4X16_LATCH_MATRIX _4x16_latch_matrix_4 (
    .IN(IN), .READ(READ), .WR(WR), .R_0(R_0), .R_1(R_1), .R_2(R_2), .R_3(R_3), .R_4(R_4), .R_5(R_5),
    .R_6(R_6), .R_7(R_7), .R_8(R_8), .R_9(R_9), .R_10(R_10), .R_11(R_11), .R_12(R_12), .R_13(R_13),
    .R_14(R_14), .R_15(R_15), .C_0(C_12), .C_1(C_13), .C_2(C_14), .C_3(C_15), .OUT(_4x16_latch_matrix_4_out));
  _4_BIT_IS_1 _4_bit_is_1_1 (
    .IN_0(_4x16_latch_matrix_4_out), .IN_1(_4x16_latch_matrix_3_out), .IN_2(_4x16_latch_matrix_2_out),
    .IN_3(_4x16_latch_matrix_1_out), .OUT(OUT));
endmodule
