// Digital circuit M_S_DFF_WITH_RESET.dig as structural Verilog
module M_S_DFF_WITH_RESET (
  input  DATA,
  input  CLK,
  input  CLEAR,
  output Q
);

  wire nand_1_out, nand_2_out, nand_3_out, nand_4_out, nand_5_out, nand_6_out, nand_7_out, nand_8_out,
       not_1_out, not_2_out, not_3_out, or_1_out;

  not not_1 (not_1_out, CLEAR);
  not not_2 (not_2_out, DATA);
  nand nand_1 (nand_1_out, DATA, CLK);
  nand nand_2 (nand_2_out, CLK, not_2_out);
  nand nand_3 (nand_3_out, nand_1_out, nand_4_out);
  nand nand_4 (nand_4_out, nand_3_out, nand_2_out);
  not not_3 (not_3_out, CLK);
  or or_1 (or_1_out, not_3_out, not_1_out);
  nand nand_5 (nand_5_out, nand_3_out, not_3_out);
  nand nand_6 (nand_6_out, not_3_out, nand_4_out);
  nand nand_7 (nand_7_out, nand_5_out, nand_8_out);
  nand nand_8 (nand_8_out, nand_7_out, nand_6_out);
  and and_1 (Q, nand_7_out, or_1_out);

  // Notes on the sheet:
  //   Master D Flip-Flop
  //   SET
  //   RESET
  //   Slave SR Flip-FLop
endmodule
