// Digital circuit ROW_7.dig as structural Verilog
module ROW_7 (
  input  B_7,
  input  HA,
  input  FA_IN,
  input  FA_IN_2,
  input  FA_IN_3,
  input  FA_IN_4,
  input  FA_IN_5,
  input  FA_IN_6,
  input  FA_IN_7,
  input  A_0,
  input  A_1,
  input  A_2,
  input  A_3,
  input  A_4,
  input  A_5,
  input  A_6,
  input  A_7,
  output P7,
  output P8,
  output P9,
  output P10,
  output P11,
  output P12,
  output P13,
  output P14,
  output P15
);

  wire and_1_out, and_2_out, and_3_out, and_4_out, and_5_out, and_6_out, and_7_out, and_8_out,
       full_adder_2_carry, full_adder_3_carry, full_adder_4_carry, full_adder_5_carry, full_adder_6_carry,
       full_adder_7_carry, half_adder_1_carry;

  and and_1 (and_1_out, A_7, B_7);
  FULL_ADDER full_adder_1 (.A(full_adder_2_carry), .B(FA_IN_7), .C(and_1_out), .SUM(P14), .CARRY(P15));
  and and_2 (and_2_out, A_6, B_7);
  FULL_ADDER full_adder_2 (.A(full_adder_3_carry), .B(FA_IN_6), .C(and_2_out), .SUM(P13), .CARRY(full_adder_2_carry));
  and and_3 (and_3_out, A_5, B_7);
  FULL_ADDER full_adder_3 (.A(full_adder_4_carry), .B(FA_IN_5), .C(and_3_out), .SUM(P12), .CARRY(full_adder_3_carry));
  and and_4 (and_4_out, A_4, B_7);
  FULL_ADDER full_adder_4 (.A(full_adder_5_carry), .B(FA_IN_4), .C(and_4_out), .SUM(P11), .CARRY(full_adder_4_carry));
  and and_5 (and_5_out, A_3, B_7);
  FULL_ADDER full_adder_5 (.A(full_adder_6_carry), .B(FA_IN_3), .C(and_5_out), .SUM(P10), .CARRY(full_adder_5_carry));
  and and_6 (and_6_out, A_2, B_7);
  FULL_ADDER full_adder_6 (.A(full_adder_7_carry), .B(FA_IN_2), .C(and_6_out), .SUM(P9), .CARRY(full_adder_6_carry));
  and and_7 (and_7_out, A_1, B_7);
  and and_8 (and_8_out, A_0, B_7);
  FULL_ADDER full_adder_7 (.A(half_adder_1_carry), .B(FA_IN), .C(and_7_out), .SUM(P8), .CARRY(full_adder_7_carry));
  HALF_ADDER half_adder_1 (.A(HA), .B(and_8_out), .SUM(P7), .CARRY(half_adder_1_carry));
endmodule
