// Digital circuit USR_RIGHT_SHIFT_UNIT.dig as structural Verilog
module USR_RIGHT_SHIFT_UNIT (
  input  S_0,
  input  S_1,
  input  SI_RIGHT_SHIFT,
  input  CLEAR,
  input  CLK,
  input  D_3,
  input  D_0,
  input  D_2,
  output Q
);

  wire _4x1_mtplx_4_regs_1_y, and_1_out;

  _4X1_MTPLX_4_REGS _4x1_mtplx_4_regs_1 (
    .D_0(D_0), .D_1(SI_RIGHT_SHIFT), .D_2(D_2), .D_3(D_3), .S_1(S_1), .S_0(S_0), .Y(_4x1_mtplx_4_regs_1_y));
  and and_1 (and_1_out, _4x1_mtplx_4_regs_1_y, CLEAR);
  MASTER_SLAVE_D_TYPE_FLIP_FLOP master_slave_d_type_flip_flop_1 (.DATA(and_1_out), .CLK(CLK), .Q(Q));
endmodule
